// Logisim project sap2.circ as structural Verilog: 33 circuits, main circuit main
// RESET
module main (
  input  PRGMODE,
  input  [7:0] DATA_INPUT,
  input  [14:0] in_3,
  input  in_4,
  input  in_5,
  output [12:0] out_6
);

  wire a0, a1, a2, abaddrsel, ALT_qn, and_2_out, and_6_out, and_7_out, and_8_out, and_10_out, and_11_out,
       and_12_out, and_13_out, and_18_out, and_21_out, and_22_out, bnk0en, bnk1en, button_1_out,
       button_2_out, clDISP, clDISPLATCH, clEnABUSReg, clEnALU, clEnBk4, clEnCons, clEnMAREG, clEnPCREG,
       clEnRAM, clEnREGA, clEnREGB, clEnREGF, clEnREGI, clEnSPREG, clEXX, CLK, clPCcount, clSource,
       clSPcntUp, clSPcount, clWAH8BUS, clWAL8BUS, clWBk4, clWMAREG, clWPCREG, clWRAM, clWREGA, clWREGB,
       clWREGF, clWREGI, clWREGO, clWSPREG, controlled_buffer_11_out, controlled_buffer_13_out,
       controlled_buffer_16_out, controlled_buffer_19_out, controlled_buffer_20_out,
       controlled_buffer_21_out, controlled_buffer_22_out, controlled_buffer_23_out, cpuCLK, cpuCLKdiv2, d1,
       d2, d3, d4, d_ff_2_q, enBnk0, enBnk1, fC, flagP, fNC, fNV, fNZ, hex7seg_1_a, hex7seg_1_b, hex7seg_1_c,
       hex7seg_1_d, hex7seg_1_dp, hex7seg_1_e, hex7seg_1_f, hex7seg_1_g, hex7seg_2_a, hex7seg_2_b,
       hex7seg_2_c, hex7seg_2_d, hex7seg_2_dp, hex7seg_2_e, hex7seg_2_f, hex7seg_2_g, hex7seg_3_a,
       hex7seg_3_b, hex7seg_3_c, hex7seg_3_d, hex7seg_3_dp, hex7seg_3_e, hex7seg_3_f, hex7seg_3_g,
       hex7seg_4_a, hex7seg_4_b, hex7seg_4_c, hex7seg_4_d, hex7seg_4_dp, hex7seg_4_e, hex7seg_4_f,
       hex7seg_4_g, hex7seg_5_a, hex7seg_5_b, hex7seg_5_c, hex7seg_5_d, hex7seg_5_dp, hex7seg_5_e,
       hex7seg_5_f, hex7seg_5_g, hex7seg_6_a, hex7seg_6_b, hex7seg_6_c, hex7seg_6_d, hex7seg_6_dp,
       hex7seg_6_e, hex7seg_6_f, hex7seg_6_g, hex7seg_7_a, hex7seg_7_b, hex7seg_7_c, hex7seg_7_d,
       hex7seg_7_dp, hex7seg_7_e, hex7seg_7_f, hex7seg_7_g, hex7seg_8_a, hex7seg_8_b, hex7seg_8_c,
       hex7seg_8_d, hex7seg_8_dp, hex7seg_8_e, hex7seg_8_f, hex7seg_8_g, hex7seg_9_a, hex7seg_9_b,
       hex7seg_9_c, hex7seg_9_d, hex7seg_9_dp, hex7seg_9_e, hex7seg_9_f, hex7seg_9_g, hex7seg_10_a,
       hex7seg_10_b, hex7seg_10_c, hex7seg_10_d, hex7seg_10_dp, hex7seg_10_e, hex7seg_10_f, hex7seg_10_g,
       hex7seg_11_a, hex7seg_11_b, hex7seg_11_c, hex7seg_11_d, hex7seg_11_dp, hex7seg_11_e, hex7seg_11_f,
       hex7seg_11_g, hex7seg_12_a, hex7seg_12_b, hex7seg_12_c, hex7seg_12_d, hex7seg_12_dp, hex7seg_12_e,
       hex7seg_12_f, hex7seg_12_g, hex7seg_13_a, hex7seg_13_b, hex7seg_13_c, hex7seg_13_d, hex7seg_13_dp,
       hex7seg_13_e, hex7seg_13_f, hex7seg_13_g, hex7seg_14_a, hex7seg_14_b, hex7seg_14_c, hex7seg_14_d,
       hex7seg_14_dp, hex7seg_14_e, hex7seg_14_f, hex7seg_14_g, hex7seg_15_a, hex7seg_15_b, hex7seg_15_c,
       hex7seg_15_d, hex7seg_15_dp, hex7seg_15_e, hex7seg_15_f, hex7seg_15_g, hex7seg_16_a, hex7seg_16_b,
       hex7seg_16_c, hex7seg_16_d, hex7seg_16_dp, hex7seg_16_e, hex7seg_16_f, hex7seg_16_g, hex7seg_17_a,
       hex7seg_17_b, hex7seg_17_c, hex7seg_17_d, hex7seg_17_dp, hex7seg_17_e, hex7seg_17_f, hex7seg_17_g,
       hex7seg_18_a, hex7seg_18_b, hex7seg_18_c, hex7seg_18_d, hex7seg_18_dp, hex7seg_18_e, hex7seg_18_f,
       hex7seg_18_g, hex7seg_19_a, hex7seg_19_b, hex7seg_19_c, hex7seg_19_d, hex7seg_19_dp, hex7seg_19_e,
       hex7seg_19_f, hex7seg_19_g, hex7seg_20_a, hex7seg_20_b, hex7seg_20_c, hex7seg_20_d, hex7seg_20_dp,
       hex7seg_20_e, hex7seg_20_f, hex7seg_20_g, hex7seg_21_a, hex7seg_21_b, hex7seg_21_c, hex7seg_21_d,
       hex7seg_21_dp, hex7seg_21_e, hex7seg_21_f, hex7seg_21_g, hex7seg_22_a, hex7seg_22_b, hex7seg_22_c,
       hex7seg_22_d, hex7seg_22_dp, hex7seg_22_e, hex7seg_22_f, hex7seg_22_g, hex7seg_23_a, hex7seg_23_b,
       hex7seg_23_c, hex7seg_23_d, hex7seg_23_dp, hex7seg_23_e, hex7seg_23_f, hex7seg_23_g, hex7seg_24_a,
       hex7seg_24_b, hex7seg_24_c, hex7seg_24_d, hex7seg_24_dp, hex7seg_24_e, hex7seg_24_f, hex7seg_24_g,
       IORdReq, ioreq, IOWrReq, Lp, multiplexer_2_out, multiplexer_3_out, nCE, nCLK, ncpuCLK, nEi, nLa, nLah,
       nLal, nLb, nLi, nLk, nLm, nLo, nLs, not_1_out, not_2_out, not_15_out, not_22_out, not_23_out,
       nPRGMODE, nPRGWR, or_3_out, pause, PRGWR, pull_resistor_25_node, pull_resistor_26_node,
       pull_resistor_47_node, pull_resistor_48_node, pull_resistor_58_node, pull_resistor_63_node, ramCLK,
       ramOE, ramWE, RESET_out, romOE, romsel, selEnRAM, selWRAM, soundunit_1_en, uRESET, wrBnk0, wrBnk1;
  wire [1:0] bkwrsel, sreg;
  wire [3:0] s1h, s1hs, s1l, s1ls, s2h, s2hs, s2l, s2ls, s3h, s3hs, s3l, s3ls, s4h, s4hs, s4l, s4ls,
       soundunit_1_vol;
  wire [3:2] memiounit_1_out_6;
  wire [4:0] FLAGBUS;
  wire [5:0] alufnc, controlled_buffer_17_out;
  wire [7:0] ABUSHreg_q, ABUSLreg_q, ADBUSH, ADBUSL, ALURBUS, AREGBUS, BREGBUS, DBUS, IREGBUS, OREGBUS,
       ROMModule_data, segdecdisplay_1_hseg;
  wire [7:1] FLAGS;
  wire [13:0] soundunit_1_frq;
  wire [14:0] SELABUS;
  wire [15:0] ABUS16, MARBUS, PCBUS, RAMABUS, SPBUS;
  wire [19:0] CONQ;
  wire [31:0] CON, DBGREGBANK0, DBGREGBANK1, rom_1_data;

  ROM #(.addrWidth(15)) ROMModule (.addr(SELABUS), .data(ROMModule_data));
  hex7seg hex7seg_1 (
    .a(hex7seg_1_a), .b(hex7seg_1_b), .c(hex7seg_1_c), .d(hex7seg_1_d), .e(hex7seg_1_e), .f(hex7seg_1_f),
    .g(hex7seg_1_g), .dp(hex7seg_1_dp), .en(pull_resistor_25_node), .value(PCBUS[15:12]));  // open: dot
  hex7seg hex7seg_2 (
    .a(hex7seg_2_a), .b(hex7seg_2_b), .c(hex7seg_2_c), .d(hex7seg_2_d), .e(hex7seg_2_e), .f(hex7seg_2_f),
    .g(hex7seg_2_g), .dp(hex7seg_2_dp), .en(pull_resistor_26_node), .value(SPBUS[15:12]));  // open: dot
  Pull_Resistor pull_resistor_1 (.node(clPCcount));
  Pull_Resistor pull_resistor_2 (.node(clEnPCREG));
  assign ADBUSL = clSource ? ABUS16[7:0] : 8'bz;  // Controlled_Buffer controlled_buffer_1
  not not_1 (not_1_out, clSource);
  assign ADBUSH = clSource ? ABUS16[15:8] : 8'bz;  // Controlled_Buffer controlled_buffer_2
  not not_2 (not_2_out, clSource);
  Register Areg (.D(ADBUSL), .en(clWREGA), .clk(cpuCLK), .Q(AREGBUS), .clr(uRESET));
  Register IReg (.D(DBUS), .en(clWREGI), .clk(cpuCLK), .Q(IREGBUS), .clr(uRESET));
  not not_3 (romsel, abaddrsel);
  _7_Segment_Display u_7_segment_display_1 (
    .g(hex7seg_1_g), .f(hex7seg_1_f), .a(hex7seg_1_a), .b(hex7seg_1_b), .e(hex7seg_1_e), .d(hex7seg_1_d),
    .c(hex7seg_1_c), .dp(hex7seg_1_dp));
  hex7seg hex7seg_3 (
    .a(hex7seg_3_a), .b(hex7seg_3_b), .c(hex7seg_3_c), .d(hex7seg_3_d), .e(hex7seg_3_e), .f(hex7seg_3_f),
    .g(hex7seg_3_g), .dp(hex7seg_3_dp), .en(pull_resistor_25_node), .value(PCBUS[11:8]));  // open: dot
  _7_Segment_Display u_7_segment_display_2 (
    .g(hex7seg_2_g), .f(hex7seg_2_f), .a(hex7seg_2_a), .b(hex7seg_2_b), .e(hex7seg_2_e), .d(hex7seg_2_d),
    .c(hex7seg_2_c), .dp(hex7seg_2_dp));
  hex7seg hex7seg_4 (
    .a(hex7seg_4_a), .b(hex7seg_4_b), .c(hex7seg_4_c), .d(hex7seg_4_d), .e(hex7seg_4_e), .f(hex7seg_4_f),
    .g(hex7seg_4_g), .dp(hex7seg_4_dp), .en(pull_resistor_26_node), .value(SPBUS[11:8]));  // open: dot
  not not_4 (clWSPREG, nLs);
  not not_5 (clWBk4, nLk);
  not not_6 (clWMAREG, nLm);
  not not_7 (clEnRAM, nCE);
  not not_8 (clWREGI, nLi);
  not not_9 (clEnREGI, nEi);
  not not_10 (clWREGA, nLa);
  not not_11 (clWREGB, nLb);
  not not_12 (clWREGO, nLo);
  not not_13 (clWAL8BUS, nLal);
  not not_14 (clWAH8BUS, nLah);
  Pull_Resistor #(.pull(1)) pull_resistor_3 (.node(nLm));
  Pull_Resistor #(.pull(1)) pull_resistor_4 (.node(nCE));
  assign ADBUSL = not_1_out ? DBUS : 8'bz;  // Controlled_Buffer controlled_buffer_3
  assign ADBUSH = not_2_out ? DBUS : 8'bz;  // Controlled_Buffer controlled_buffer_4
  Register ABUSLreg (.D(DBUS), .en(clWAL8BUS), .clk(cpuCLK), .Q(ABUSLreg_q), .clr(uRESET));
  Register ABUSHreg (.D(DBUS), .en(clWAH8BUS), .clk(cpuCLK), .Q(ABUSHreg_q), .clr(uRESET));
  assign DBUS = clEnREGA ? AREGBUS : 8'bz;  // Controlled_Buffer controlled_buffer_5
  Pull_Resistor pull_resistor_5 (.node(clEnREGA));
  assign DBUS = clEnREGI ? IREGBUS : 8'bz;  // Controlled_Buffer controlled_buffer_6
  Pull_Resistor pull_resistor_6 (.node(clEnREGI));
  constantbank constantbank_1 (.Q(DBUS), .regsel({a2, a1, a0}), .en(clEnCons));
  Multiplexer #(.enable("false"), .select(3), .width(6)) multiplexer_1 (
    .in0(6'b001100), .in1(6'b000011), .in2(6'b111000), .in3(6'b111110), .in4(6'b110110), .in5(6'b010000),
    .in6(6'b100000), .in7({6{1'b0}}), .out(alufnc), .sel({a2, a1, a0}));
  // Probe on {abaddrsel, SELABUS}
  _7_Segment_Display u_7_segment_display_3 (
    .g(hex7seg_3_g), .f(hex7seg_3_f), .a(hex7seg_3_a), .b(hex7seg_3_b), .e(hex7seg_3_e), .d(hex7seg_3_d),
    .c(hex7seg_3_c), .dp(hex7seg_3_dp));
  _7_Segment_Display u_7_segment_display_4 (
    .g(hex7seg_4_g), .f(hex7seg_4_f), .a(hex7seg_4_a), .b(hex7seg_4_b), .e(hex7seg_4_e), .d(hex7seg_4_d),
    .c(hex7seg_4_c), .dp(hex7seg_4_dp));
  Pull_Resistor #(.pull(1)) pull_resistor_7 (.node(nLi));
  Pull_Resistor #(.pull(1)) pull_resistor_8 (.node(nEi));
  Pull_Resistor pull_resistor_9 (.node(clDISPLATCH));
  assign ABUS16[7:0] = clEnABUSReg ? ABUSLreg_q : 8'bz;  // Controlled_Buffer controlled_buffer_7
  Pull_Resistor pull_resistor_10 (.node(clEnABUSReg));
  assign ABUS16[15:8] = clEnABUSReg ? ABUSHreg_q : 8'bz;  // Controlled_Buffer controlled_buffer_8
  Pull_Resistor pull_resistor_11 (.node(clEnABUSReg));
  Pull_Resistor pull_resistor_12 (.node(ramWE));
  // Probe on IREGBUS
  _7_Segment_Display u_7_segment_display_5 (
    .g(hex7seg_5_g), .f(hex7seg_5_f), .a(hex7seg_5_a), .b(hex7seg_5_b), .e(hex7seg_5_e), .d(hex7seg_5_d),
    .c(hex7seg_5_c), .dp(hex7seg_5_dp));
  hex7seg hex7seg_5 (
    .a(hex7seg_5_a), .b(hex7seg_5_b), .c(hex7seg_5_c), .d(hex7seg_5_d), .e(hex7seg_5_e), .f(hex7seg_5_f),
    .g(hex7seg_5_g), .dp(hex7seg_5_dp), .en(pull_resistor_25_node), .value(PCBUS[7:4]));  // open: dot
  _7_Segment_Display u_7_segment_display_6 (
    .g(hex7seg_6_g), .f(hex7seg_6_f), .a(hex7seg_6_a), .b(hex7seg_6_b), .e(hex7seg_6_e), .d(hex7seg_6_d),
    .c(hex7seg_6_c), .dp(hex7seg_6_dp));
  hex7seg hex7seg_6 (
    .a(hex7seg_6_a), .b(hex7seg_6_b), .c(hex7seg_6_c), .d(hex7seg_6_d), .e(hex7seg_6_e), .f(hex7seg_6_f),
    .g(hex7seg_6_g), .dp(hex7seg_6_dp), .en(pull_resistor_26_node), .value(SPBUS[7:4]));  // open: dot
  LED led_1 (.in(clPCcount));
  LED led_2 (.in(clEnPCREG));
  LED led_3 (.in(nLm));
  Pull_Resistor #(.pull(1)) pull_resistor_13 (.node(nLa));
  Pull_Resistor pull_resistor_14 (.node(clEnREGA));
  Pull_Resistor pull_resistor_15 (.node(clDISP));
  Pull_Resistor pull_resistor_16 (.node(clEnABUSReg));
  Pull_Resistor pull_resistor_17 (.node(clEnREGF));
  Register Breg (.D(ADBUSH), .en(clWREGB), .clk(cpuCLK), .Q(BREGBUS), .clr(uRESET));
  Register OReg (.D(DBUS), .en(clWREGO), .clk(cpuCLK), .Q(OREGBUS), .clr(uRESET));
  RAM #(.addrWidth(15), .asyncread("true"), .databus("bidir"), .\type ("nonvolatile")) ram_1 (
    .addr(SELABUS), .we(ramWE), .oe(ramOE), .clk(ramCLK), .data(DBUS));
  and and_1 (romOE, romsel, not_15_out);
  not not_15 (not_15_out, selWRAM);
  _7_Segment_Display u_7_segment_display_7 (
    .g(hex7seg_7_g), .f(hex7seg_7_f), .a(hex7seg_7_a), .b(hex7seg_7_b), .e(hex7seg_7_e), .d(hex7seg_7_d),
    .c(hex7seg_7_c), .dp(hex7seg_7_dp));
  hex7seg hex7seg_7 (
    .a(hex7seg_7_a), .b(hex7seg_7_b), .c(hex7seg_7_c), .d(hex7seg_7_d), .e(hex7seg_7_e), .f(hex7seg_7_f),
    .g(hex7seg_7_g), .dp(hex7seg_7_dp), .en(pull_resistor_25_node), .value(PCBUS[3:0]));  // open: dot
  _7_Segment_Display u_7_segment_display_8 (
    .g(hex7seg_8_g), .f(hex7seg_8_f), .a(hex7seg_8_a), .b(hex7seg_8_b), .e(hex7seg_8_e), .d(hex7seg_8_d),
    .c(hex7seg_8_c), .dp(hex7seg_8_dp));
  hex7seg hex7seg_8 (
    .a(hex7seg_8_a), .b(hex7seg_8_b), .c(hex7seg_8_c), .d(hex7seg_8_d), .e(hex7seg_8_e), .f(hex7seg_8_f),
    .g(hex7seg_8_g), .dp(hex7seg_8_dp), .en(pull_resistor_26_node), .value(SPBUS[3:0]));  // open: dot
  // Probe on CONQ
  LED led_4 (.in(nCE));
  Pull_Resistor pull_resistor_18 (.node(clEnREGB));
  Pull_Resistor pull_resistor_19 (.node(clEnALU));
  Pull_Resistor #(.pull(1)) pull_resistor_20 (.node(nLb));
  Pull_Resistor pull_resistor_21 (.node(clEnCons));
  Pull_Resistor pull_resistor_22 (.node(clWSPREG));
  Pull_Resistor pull_resistor_23 (.node(clEnSPREG));
  assign DBUS = clEnREGB ? BREGBUS : 8'bz;  // Controlled_Buffer controlled_buffer_9
  Pull_Resistor pull_resistor_24 (.node(clEnREGB));
  assign DBUS = romOE ? ROMModule_data : 8'bz;  // Controlled_Buffer controlled_buffer_10
  controller controller_1 (
    .Q(CONQ), .addr(out_6), .cntrl(CON), .cpuCLK(cpuCLK), .ncpuCLK(ncpuCLK), .CLK(CLK), .nCLK(nCLK),
    .clkd2(cpuCLKdiv2), .pause(PRGMODE), .clr(uRESET), .opcode(IREGBUS));  // open: opdec
  LED led_5 (.in(CONQ[0]));
  LED led_6 (.in(CONQ[1]));
  LED led_7 (.in(CONQ[2]));
  LED led_8 (.in(CONQ[3]));
  LED led_9 (.in(CONQ[4]));
  LED led_10 (.in(CONQ[5]));
  LED led_11 (.in(CONQ[6]));
  LED led_12 (.in(CONQ[7]));
  Pull_Resistor #(.pull(1)) pull_resistor_25 (.node(pull_resistor_25_node));
  LED led_13 (.in(CONQ[8]));
  LED led_14 (.in(CONQ[9]));
  LED led_15 (.in(CONQ[10]));
  LED led_16 (.in(CONQ[11]));
  LED led_17 (.in(CONQ[12]));
  LED led_18 (.in(CONQ[13]));
  LED led_19 (.in(CONQ[14]));
  LED led_20 (.in(CONQ[15]));
  LED led_21 (.in(CONQ[16]));
  LED led_22 (.in(CONQ[17]));
  LED led_23 (.in(CONQ[18]));
  LED led_24 (.in(CONQ[19]));
  Pull_Resistor #(.pull(1)) pull_resistor_26 (.node(pull_resistor_26_node));
  // Probe on CON
  LED led_25 (.in(nLi));
  LED led_26 (.in(nEi));
  LED led_27 (.in(nLa));
  LED led_28 (.in(clEnREGA));
  Pull_Resistor #(.pull(1)) pull_resistor_27 (.node(nLo));
  Pull_Resistor pull_resistor_28 (.node(clWRAM));
  Pull_Resistor pull_resistor_29 (.node(Lp));
  Pull_Resistor pull_resistor_30 (.node(clWAL8BUS));
  Pull_Resistor pull_resistor_31 (.node(clWAH8BUS));
  // Probe on ABUS16
  alu alu_1 (
    .res(ALURBUS), .C(FLAGBUS[0]), .Z(FLAGBUS[1]), .P(FLAGBUS[2]), .V(FLAGBUS[3]), .S(FLAGBUS[4]),
    .A(AREGBUS), .B(BREGBUS), .cin(fC), .en(1'b1), .fn(alufnc));
  // Probe on CONQ
  // Probe on out_6
  hex7seg hex7seg_9 (
    .a(hex7seg_9_a), .b(hex7seg_9_b), .c(hex7seg_9_c), .d(hex7seg_9_d), .e(hex7seg_9_e), .f(hex7seg_9_f),
    .g(hex7seg_9_g), .dp(hex7seg_9_dp), .en(pull_resistor_47_node), .value(AREGBUS[7:4]));  // open: dot
  hex7seg hex7seg_10 (
    .a(hex7seg_10_a), .b(hex7seg_10_b), .c(hex7seg_10_c), .d(hex7seg_10_d), .e(hex7seg_10_e),
    .f(hex7seg_10_f), .g(hex7seg_10_g), .dp(hex7seg_10_dp), .en(pull_resistor_48_node), .value(BREGBUS[7:4]));  // open: dot
  and and_2 (and_2_out, ~alufnc[5], ~alufnc[4], alufnc[3], alufnc[2], ~alufnc[1], ~alufnc[0]);  // AND_Gate
  assign controlled_buffer_11_out = clEnALU ? and_2_out : 1'bz;  // Controlled_Buffer controlled_buffer_11
  LED led_29 (.in(controlled_buffer_11_out));
  LED led_30 (.in(clEnREGB));
  Pull_Resistor pull_resistor_32 (.node(a1));
  Pull_Resistor pull_resistor_33 (.node(a0));
  Button button_1 (.out(button_1_out));
  Pull_Resistor pull_resistor_34 (.node(clWBk4));
  Register #(.width(16)) MAReg (.D(ABUS16), .en(clWMAREG), .clk(cpuCLK), .Q(MARBUS), .clr(uRESET));
  Register Freg (
    .D({3'b000, FLAGBUS}), .en(clWREGF), .clk(cpuCLK), .Q({FLAGS[7:3], flagP, FLAGS[1], fC}), .clr(uRESET));
  assign DBUS = clEnREGF ? {FLAGS[7:3], flagP, FLAGS[1], fC} : 8'bz;  // Controlled_Buffer controlled_buffer_12
  Pull_Resistor pull_resistor_35 (.node(clEnREGF));
  // Probe on DBUS
  and and_3 (IOWrReq, selWRAM, romsel);
  and and_4 (ramWE, selWRAM, abaddrsel);
  and and_5 (ramOE, selEnRAM, abaddrsel);
  _7_Segment_Display u_7_segment_display_9 (
    .g(hex7seg_9_g), .f(hex7seg_9_f), .a(hex7seg_9_a), .b(hex7seg_9_b), .e(hex7seg_9_e), .d(hex7seg_9_d),
    .c(hex7seg_9_c), .dp(hex7seg_9_dp));
  _7_Segment_Display u_7_segment_display_10 (
    .g(hex7seg_10_g), .f(hex7seg_10_f), .a(hex7seg_10_a), .b(hex7seg_10_b), .e(hex7seg_10_e),
    .d(hex7seg_10_d), .c(hex7seg_10_c), .dp(hex7seg_10_dp));
  and and_6 (and_6_out, ~alufnc[5], ~alufnc[4], ~alufnc[3], ~alufnc[2], alufnc[1], alufnc[0]);  // AND_Gate
  assign controlled_buffer_13_out = clEnALU ? and_6_out : 1'bz;  // Controlled_Buffer controlled_buffer_13
  LED led_31 (.in(controlled_buffer_13_out));
  LED led_32 (.in(clEnALU));
  LED led_33 (.in(nLb));
  LED led_34 (.in(nLo));
  Pull_Resistor pull_resistor_36 (.node(nLal));
  Pull_Resistor pull_resistor_37 (.node(nLah));
  Pull_Resistor pull_resistor_38 (.node(clEnABUSReg));
  toggleswitch toggleswitch_1 (.switch(pause), .clk(CLK), .res(uRESET), .I(button_1_out));  // open: latch
  Pull_Resistor pull_resistor_39 (.node(bkwrsel[0]));
  Pull_Resistor pull_resistor_40 (.node(bkwrsel[1]));
  Pull_Resistor pull_resistor_41 (.node(a0));
  Pull_Resistor pull_resistor_42 (.node(a1));
  // Probe on RAMABUS
  assign RAMABUS = clEnMAREG ? MARBUS : 16'bz;  // Controlled_Buffer controlled_buffer_14
  Pull_Resistor #(.pull(1)) pull_resistor_43 (.node(clEnMAREG));
  // Probe on {FLAGS[7:3], flagP, FLAGS[1], fC}
  // Probe on controlled_buffer_17_out
  assign {clPCcount, clEnPCREG, nLm, nCE, nLi, nEi, nLa, clEnREGA, clEnREGB, clEnALU, nLb, nLo, clWRAM, Lp, a1, a0, nLal, nLah, clEnABUSReg, clWREGF, clEnBk4, nLk, bkwrsel, a2, clEnCons, clEXX, clSource, clSPcntUp, clEnSPREG, clSPcount, nLs} = nPRGMODE ? CON : 32'bz;  // Controlled_Buffer controlled_buffer_15
  _7_Segment_Display u_7_segment_display_11 (
    .g(hex7seg_11_g), .f(hex7seg_11_f), .a(hex7seg_11_a), .b(hex7seg_11_b), .e(hex7seg_11_e),
    .d(hex7seg_11_d), .c(hex7seg_11_c), .dp(hex7seg_11_dp));
  hex7seg hex7seg_11 (
    .a(hex7seg_11_a), .b(hex7seg_11_b), .c(hex7seg_11_c), .d(hex7seg_11_d), .e(hex7seg_11_e),
    .f(hex7seg_11_f), .g(hex7seg_11_g), .dp(hex7seg_11_dp), .en(pull_resistor_47_node), .value(AREGBUS[3:0]));  // open: dot
  _7_Segment_Display u_7_segment_display_12 (
    .g(hex7seg_12_g), .f(hex7seg_12_f), .a(hex7seg_12_a), .b(hex7seg_12_b), .e(hex7seg_12_e),
    .d(hex7seg_12_d), .c(hex7seg_12_c), .dp(hex7seg_12_dp));
  hex7seg hex7seg_12 (
    .a(hex7seg_12_a), .b(hex7seg_12_b), .c(hex7seg_12_c), .d(hex7seg_12_d), .e(hex7seg_12_e),
    .f(hex7seg_12_f), .g(hex7seg_12_g), .dp(hex7seg_12_dp), .en(pull_resistor_48_node), .value(BREGBUS[3:0]));  // open: dot
  and and_7 (and_7_out, alufnc[5], ~alufnc[4], ~alufnc[3], ~alufnc[2], ~alufnc[1], ~alufnc[0]);  // AND_Gate
  assign controlled_buffer_16_out = clEnALU ? and_7_out : 1'bz;  // Controlled_Buffer controlled_buffer_16
  LED led_35 (.in(controlled_buffer_16_out));
  // Probe on MARBUS
  // Probe on PCBUS
  // Probe on ABUS16
  // Probe on DBUS
  // Probe on IREGBUS
  // Probe on RAMABUS
  LED led_36 (.in(clWRAM));
  LED led_37 (.in(Lp));
  LED led_38 (.in(a1));
  Pull_Resistor pull_resistor_44 (.node(clWREGF));
  Pull_Resistor pull_resistor_45 (.node(clEnBk4));
  Pull_Resistor #(.pull(1)) pull_resistor_46 (.node(nLk));
  LED led_39 (.in(pause));
  // Probe on ABUS16
  assign controlled_buffer_17_out = clEnALU ? alufnc : 6'bz;  // Controlled_Buffer controlled_buffer_17
  assign DBUS = clEnALU ? ALURBUS : 8'bz;  // Controlled_Buffer controlled_buffer_18
  LED led_40 (.in(FLAGBUS[0]));
  LED led_41 (.in(FLAGBUS[1]));
  LED led_42 (.in(FLAGBUS[2]));
  LED led_43 (.in(FLAGBUS[3]));
  LED led_44 (.in(FLAGBUS[4]));
  hex7seg hex7seg_13 (
    .a(hex7seg_13_a), .b(hex7seg_13_b), .c(hex7seg_13_c), .d(hex7seg_13_d), .e(hex7seg_13_e),
    .f(hex7seg_13_f), .g(hex7seg_13_g), .dp(hex7seg_13_dp), .en(pull_resistor_58_node), .value(IREGBUS[7:4]));  // open: dot
  Pull_Resistor #(.pull(1)) pull_resistor_47 (.node(pull_resistor_47_node));
  hex7seg hex7seg_14 (
    .a(hex7seg_14_a), .b(hex7seg_14_b), .c(hex7seg_14_c), .d(hex7seg_14_d), .e(hex7seg_14_e),
    .f(hex7seg_14_f), .g(hex7seg_14_g), .dp(hex7seg_14_dp), .en(pull_resistor_63_node), .value(OREGBUS[7:4]));  // open: dot
  Pull_Resistor #(.pull(1)) pull_resistor_48 (.node(pull_resistor_48_node));
  and and_8 (and_8_out, ~alufnc[5], alufnc[4], ~alufnc[3], ~alufnc[2], ~alufnc[1], ~alufnc[0]);  // AND_Gate
  assign controlled_buffer_19_out = clEnALU ? and_8_out : 1'bz;  // Controlled_Buffer controlled_buffer_19
  LED led_45 (.in(controlled_buffer_19_out));
  LED led_46 (.in(a0));
  LED led_47 (.in(nLal));
  LED led_48 (.in(nLah));
  Pull_Resistor pull_resistor_49 (.node(bkwrsel[1]));
  Pull_Resistor pull_resistor_50 (.node(bkwrsel[0]));
  Pull_Resistor pull_resistor_51 (.node(a2));
  Pull_Resistor pull_resistor_52 (.node(a2));
  Pull_Resistor pull_resistor_53 (.node(a1));
  LED led_49 (.in(IOWrReq));
  LED led_50 (.in(IORdReq));
  and and_9 (IORdReq, selEnRAM, romsel);
  // Probe on {clPCcount, clEnPCREG, nLm, nCE, nLi, nEi, nLa, clEnREGA, clEnREGB, clEnALU, nLb, nLo, clWRAM, Lp, a1, a0, nLal, nLah, clEnABUSReg, clWREGF, clEnBk4, nLk, bkwrsel, a2, clEnCons, clEXX, clSource, clSPcntUp, clEnSPREG, clSPcount, nLs}
  // Probe on DBGREGBANK0
  // Probe on DBGREGBANK1
  _7_Segment_Display u_7_segment_display_13 (
    .g(hex7seg_13_g), .f(hex7seg_13_f), .a(hex7seg_13_a), .b(hex7seg_13_b), .e(hex7seg_13_e),
    .d(hex7seg_13_d), .c(hex7seg_13_c), .dp(hex7seg_13_dp));
  hex7seg hex7seg_15 (
    .a(hex7seg_15_a), .b(hex7seg_15_b), .c(hex7seg_15_c), .d(hex7seg_15_d), .e(hex7seg_15_e),
    .f(hex7seg_15_f), .g(hex7seg_15_g), .dp(hex7seg_15_dp), .en(pull_resistor_58_node), .value(IREGBUS[3:0]));  // open: dot
  _7_Segment_Display u_7_segment_display_14 (
    .g(hex7seg_14_g), .f(hex7seg_14_f), .a(hex7seg_14_a), .b(hex7seg_14_b), .e(hex7seg_14_e),
    .d(hex7seg_14_d), .c(hex7seg_14_c), .dp(hex7seg_14_dp));
  and and_10 (and_10_out, alufnc[5], alufnc[4], alufnc[3], ~alufnc[2], ~alufnc[1], ~alufnc[0]);  // AND_Gate
  assign controlled_buffer_20_out = clEnALU ? and_10_out : 1'bz;  // Controlled_Buffer controlled_buffer_20
  LED led_51 (.in(controlled_buffer_20_out));
  // Probe on SPBUS
  LED led_52 (.in(clEnABUSReg));
  LED led_53 (.in(clWREGF));
  Pull_Resistor pull_resistor_54 (.node(clEnCons));
  Pull_Resistor pull_resistor_55 (.node(clEXX));
  Pull_Resistor pull_resistor_56 (.node(clSource));
  Button button_2 (.out(button_2_out));
  Pull_Resistor pull_resistor_57 (.node(a0));
  _7_Segment_Display u_7_segment_display_15 (
    .g(hex7seg_15_g), .f(hex7seg_15_f), .a(hex7seg_15_a), .b(hex7seg_15_b), .e(hex7seg_15_e),
    .d(hex7seg_15_d), .c(hex7seg_15_c), .dp(hex7seg_15_dp));
  Pull_Resistor #(.pull(1)) pull_resistor_58 (.node(pull_resistor_58_node));
  _7_Segment_Display u_7_segment_display_16 (
    .g(hex7seg_16_g), .f(hex7seg_16_f), .a(hex7seg_16_a), .b(hex7seg_16_b), .e(hex7seg_16_e),
    .d(hex7seg_16_d), .c(hex7seg_16_c), .dp(hex7seg_16_dp));
  hex7seg hex7seg_16 (
    .a(hex7seg_16_a), .b(hex7seg_16_b), .c(hex7seg_16_c), .d(hex7seg_16_d), .e(hex7seg_16_e),
    .f(hex7seg_16_f), .g(hex7seg_16_g), .dp(hex7seg_16_dp), .en(pull_resistor_63_node), .value(OREGBUS[3:0]));  // open: dot
  and and_11 (and_11_out, alufnc[5], alufnc[4], alufnc[3], alufnc[2], alufnc[1], ~alufnc[0]);  // AND_Gate
  assign controlled_buffer_21_out = clEnALU ? and_11_out : 1'bz;  // Controlled_Buffer controlled_buffer_21
  LED led_54 (.in(controlled_buffer_21_out));
  // Probe on DBGREGBANK0
  // Probe on DBGREGBANK1
  LED led_55 (.in(clEnBk4));
  LED led_56 (.in(nLk));
  LED led_57 (.in(bkwrsel[1]));
  LED led_58 (.in(bkwrsel[0]));
  Pull_Resistor pull_resistor_59 (.node(clSPcntUp));
  Pull_Resistor pull_resistor_60 (.node(clEnSPREG));
  Pull_Resistor pull_resistor_61 (.node(clSPcount));
  Pull_Resistor #(.pull(1)) pull_resistor_62 (.node(nLs));
  toggleswitch toggleswitch_2 (.switch(clDISP), .latch(clDISPLATCH), .clk(CLK), .res(uRESET), .I(button_2_out));
  D_Flip_Flop ALT (.D(ALT_qn), .clk(clEXX), .Q(bnk1en), .Qn(ALT_qn), .reset(uRESET));  // open: preset
  hex7seg hex7seg_17 (
    .a(hex7seg_17_a), .b(hex7seg_17_b), .c(hex7seg_17_c), .d(hex7seg_17_d), .e(hex7seg_17_e),
    .f(hex7seg_17_f), .g(hex7seg_17_g), .dp(hex7seg_17_dp), .en(PRGMODE), .value(DATA_INPUT[7:4]));  // open: dot
  Pull_Resistor #(.pull(1)) pull_resistor_63 (.node(pull_resistor_63_node));
  and and_12 (and_12_out, alufnc[5], alufnc[4], ~alufnc[3], alufnc[2], alufnc[1], ~alufnc[0]);  // AND_Gate
  assign controlled_buffer_22_out = clEnALU ? and_12_out : 1'bz;  // Controlled_Buffer controlled_buffer_22
  LED led_59 (.in(controlled_buffer_22_out));
  LED led_60 (.in(a2));
  LED led_61 (.in(clEnCons));
  LED led_62 (.in(clDISP));
  // Probe on SPBUS
  stackreg SPReg (
    .Dout(ABUS16), .dbg(SPBUS), .ndwn(clSPcntUp), .Din(ABUS16), .counten(clSPcount), .reset(uRESET),
    .load(clWSPREG), .clk(cpuCLK), .pcout(clEnSPREG));
  pcreg pcreg_1 (
    .Dout(ABUS16), .dbg(PCBUS), .Din(ABUS16), .counten(clPCcount), .reset(uRESET), .load(clWPCREG),
    .clk(ncpuCLK), .pcout(clEnPCREG));
  not not_16 (bnk0en, bnk1en);
  reg4bank BankRegisters0 (
    .out_9(DBGREGBANK0), .Q(DBUS), .res(uRESET), .we(wrBnk0), .wesel(bkwrsel), .en(enBnk0),
    .regsel({a1, a0}), .clk(cpuCLK), .I(DBUS));
  reg4bank BankRegisters1 (
    .out_9(DBGREGBANK1), .Q(DBUS), .res(uRESET), .we(wrBnk1), .wesel(bkwrsel), .en(enBnk1),
    .regsel({a1, a0}), .clk(cpuCLK), .I(DBUS));
  LED led_63 (.in(PRGMODE));
  _7_Segment_Display u_7_segment_display_17 (
    .g(hex7seg_17_g), .f(hex7seg_17_f), .a(hex7seg_17_a), .b(hex7seg_17_b), .e(hex7seg_17_e),
    .d(hex7seg_17_d), .c(hex7seg_17_c), .dp(hex7seg_17_dp));
  D_Flip_Flop d_ff_1 (.D(clDISP), .clk(clDISPLATCH), .reset(uRESET));  // open: Q, Qn, preset
  _7_Segment_Display digit4 (
    .g(s4h[3]), .f(s4h[2]), .a(s4h[1]), .b(s4h[0]), .e(s4l[3]), .d(s4l[2]), .c(s4l[1]), .dp(s4l[0]));
  // Probe on {FLAGS[7:3], flagP, FLAGS[1], fC}
  // Probe on alufnc
  and and_13 (and_13_out, ~alufnc[5], ~alufnc[4], ~alufnc[3], ~alufnc[2], ~alufnc[1], ~alufnc[0]);  // AND_Gate
  assign controlled_buffer_23_out = clEnALU ? and_13_out : 1'bz;  // Controlled_Buffer controlled_buffer_23
  LED led_64 (.in(controlled_buffer_23_out));
  LED led_65 (.in(clEXX));
  LED led_66 (.in(clSource));
  LED led_67 (.in(clSPcntUp));
  // Probe on PCBUS
  LED #(.active("false")) led_68 (.in(PRGMODE));
  _7_Segment_Display u_7_segment_display_18 (
    .g(hex7seg_18_g), .f(hex7seg_18_f), .a(hex7seg_18_a), .b(hex7seg_18_b), .e(hex7seg_18_e),
    .d(hex7seg_18_d), .c(hex7seg_18_c), .dp(hex7seg_18_dp));
  hex7seg hex7seg_18 (
    .a(hex7seg_18_a), .b(hex7seg_18_b), .c(hex7seg_18_c), .d(hex7seg_18_d), .e(hex7seg_18_e),
    .f(hex7seg_18_f), .g(hex7seg_18_g), .dp(hex7seg_18_dp), .en(PRGMODE), .value(DATA_INPUT[3:0]));  // open: dot
  // Probe on DBUS
  // Probe on sreg
  memIOunit memiounit_1 (
    .dout(DBUS), .out_6({memiounit_1_out_6, sreg}), .out_7(ioreq), .IOWrReq(IOWrReq), .IORdReq(IORdReq),
    .din(DBUS), .addr({abaddrsel, SELABUS}));
  LED led_69 (.in(ioreq));
  _7_Segment_Display digit3 (
    .g(s3h[3]), .f(s3h[2]), .a(s3h[1]), .b(s3h[0]), .e(s3l[3]), .d(s3l[2]), .c(s3l[1]), .dp(s3l[0]));
  _7_Segment_Display digit2 (
    .g(s2h[3]), .f(s2h[2]), .a(s2h[1]), .b(s2h[0]), .e(s2l[3]), .d(s2l[2]), .c(s2l[1]), .dp(s2l[0]));
  LED led_70 (.in(clEnSPREG));
  LED led_71 (.in(clSPcount));
  LED led_72 (.in(nLs));
  // Probe on DBGREGBANK0
  Button WRITE (.out(PRGWR));
  // Probe on soundunit_1_vol
  _7_Segment_Display digit1 (
    .g(s1h[3]), .f(s1h[2]), .a(s1h[1]), .b(s1h[0]), .e(s1l[3]), .d(s1l[2]), .c(s1l[1]), .dp(s1l[0]));
  // Probe on {FLAGS[7:3], flagP, FLAGS[1], fC}
  and and_14 (enBnk0, clEnBk4, bnk0en);
  and and_15 (enBnk1, clEnBk4, bnk1en);
  and and_16 (wrBnk0, clWBk4, bnk0en);
  and and_17 (wrBnk1, clWBk4, bnk1en);
  // Probe on DBGREGBANK1
  _7_Segment_Display u_7_segment_display_19 (
    .g(hex7seg_19_g), .f(hex7seg_19_f), .a(hex7seg_19_a), .b(hex7seg_19_b), .e(hex7seg_19_e),
    .d(hex7seg_19_d), .c(hex7seg_19_c), .dp(hex7seg_19_dp));
  hex7seg hex7seg_19 (
    .a(hex7seg_19_a), .b(hex7seg_19_b), .c(hex7seg_19_c), .d(hex7seg_19_d), .e(hex7seg_19_e),
    .f(hex7seg_19_f), .g(hex7seg_19_g), .dp(hex7seg_19_dp), .en(PRGMODE), .value({in_4, in_3[14:12]}));  // open: dot
  // Probe on soundunit_1_en
  // Probe on soundunit_1_frq
  // Probe on {d4, d3, d2, d1}
  segdecdisplay segdecdisplay_1 (
    .reset(uRESET), .clk(CLK), .value(OREGBUS), .sign(1'b0), .en(1'b1), .anode({d4, d3, d2, d1}),
    .hseg(segdecdisplay_1_hseg));
  _7_Segment_Display u_7_segment_display_20 (
    .g(s4hs[3]), .f(s4hs[2]), .a(s4hs[1]), .b(s4hs[0]), .e(s4ls[3]), .d(s4ls[2]), .c(s4ls[1]), .dp(s4ls[0]));
  // Digital_Oscilloscope digital_oscilloscope_1: pin names not known; wires that end beside it: cpuCLK, CONQ[0], CONQ[1]
  // Digital_Oscilloscope digital_oscilloscope_2: pin names not known; wires that end beside it: alufnc[0], alufnc[5], alufnc[4], alufnc[3], alufnc[2], alufnc[1], alufnc[0], CONQ[2], cpuCLK, CONQ[3], CONQ[4], CONQ[5]
  not not_17 (fNC, fC);
  not not_18 (fNZ, FLAGS[1]);
  not not_19 (fNV, FLAGS[3]);
  hex7seg hex7seg_20 (
    .a(hex7seg_20_a), .b(hex7seg_20_b), .c(hex7seg_20_c), .d(hex7seg_20_d), .e(hex7seg_20_e),
    .f(hex7seg_20_f), .g(hex7seg_20_g), .dp(hex7seg_20_dp), .en(PRGMODE), .value(in_3[11:8]));  // open: dot
  soundunit soundunit_1 (
    .frq(soundunit_1_frq), .vol(soundunit_1_vol), .en(soundunit_1_en), .wr(ioreq), .sreg(sreg),
    .reset(uRESET), .din(DBUS));
  assign {s1h, s1l} = d1 ? segdecdisplay_1_hseg : 8'bz;  // Controlled_Buffer controlled_buffer_24
  assign {s2h, s2l} = d2 ? segdecdisplay_1_hseg : 8'bz;  // Controlled_Buffer controlled_buffer_25
  assign {s3h, s3l} = d3 ? segdecdisplay_1_hseg : 8'bz;  // Controlled_Buffer controlled_buffer_26
  assign {s4h, s4l} = d4 ? segdecdisplay_1_hseg : 8'bz;  // Controlled_Buffer controlled_buffer_27
  _7_Segment_Display u_7_segment_display_21 (
    .g(s3hs[3]), .f(s3hs[2]), .a(s3hs[1]), .b(s3hs[0]), .e(s3ls[3]), .d(s3ls[2]), .c(s3ls[1]), .dp(s3ls[0]));
  _7_Segment_Display u_7_segment_display_22 (
    .g(s2hs[3]), .f(s2hs[2]), .a(s2hs[1]), .b(s2hs[0]), .e(s2ls[3]), .d(s2ls[2]), .c(s2ls[1]), .dp(s2ls[0]));
  not not_20 (nPRGMODE, PRGMODE);
  _7_Segment_Display u_7_segment_display_23 (
    .g(hex7seg_20_g), .f(hex7seg_20_f), .a(hex7seg_20_a), .b(hex7seg_20_b), .e(hex7seg_20_e),
    .d(hex7seg_20_d), .c(hex7seg_20_c), .dp(hex7seg_20_dp));
  _7_Segment_Display u_7_segment_display_24 (
    .g(s1hs[3]), .f(s1hs[2]), .a(s1hs[1]), .b(s1hs[0]), .e(s1ls[3]), .d(s1ls[2]), .c(s1ls[1]), .dp(s1ls[0]));
  // Probe on {FLAGS[7:3], flagP, FLAGS[1], fC}
  hex7seg hex7seg_21 (
    .a(hex7seg_21_a), .b(hex7seg_21_b), .c(hex7seg_21_c), .d(hex7seg_21_d), .e(hex7seg_21_e),
    .f(hex7seg_21_f), .g(hex7seg_21_g), .dp(hex7seg_21_dp), .en(PRGMODE), .value(in_3[7:4]));  // open: dot
  assign DBUS = and_18_out ? DATA_INPUT : 8'bz;  // Controlled_Buffer controlled_buffer_28
  and and_18 (and_18_out, PRGMODE, PRGWR);
  not not_21 (nPRGWR, PRGWR);
  not not_22 (not_22_out, FLAGS[1]);
  not not_23 (not_23_out, fC);
  Multiplexer #(.enable("false"), .select(3)) multiplexer_2 (
    .in0(fC), .in1(fNZ), .in2(fNC), .in3(1'b1), .in4(FLAGS[3]), .in5(FLAGS[1]), .in6(fNV), .in7(FLAGS[4]),
    .out(multiplexer_2_out), .sel({bkwrsel[0], a1, a0}));
  _7_Segment_Display u_7_segment_display_25 (
    .g(hex7seg_21_g), .f(hex7seg_21_f), .a(hex7seg_21_a), .b(hex7seg_21_b), .e(hex7seg_21_e),
    .d(hex7seg_21_d), .c(hex7seg_21_c), .dp(hex7seg_21_dp));
  Multiplexer #(.enable("false"), .select(2)) multiplexer_3 (
    .in0(fC), .in1(not_22_out), .in2(not_23_out), .in3(1'b1), .out(multiplexer_3_out), .sel({a1, a0}));
  // AND_Gate and_19 has open pins: in0=multiplexer_3_out, in1=Lp, out=open
  and and_20 (clWPCREG, multiplexer_2_out, Lp);
  Button RESET (.out(RESET_out));
  _7_Segment_Display u_7_segment_display_26 (
    .g(hex7seg_22_g), .f(hex7seg_22_f), .a(hex7seg_22_a), .b(hex7seg_22_b), .e(hex7seg_22_e),
    .d(hex7seg_22_d), .c(hex7seg_22_c), .dp(hex7seg_22_dp));
  hex7seg hex7seg_22 (
    .a(hex7seg_22_a), .b(hex7seg_22_b), .c(hex7seg_22_c), .d(hex7seg_22_d), .e(hex7seg_22_e),
    .f(hex7seg_22_f), .g(hex7seg_22_g), .dp(hex7seg_22_dp), .en(PRGMODE), .value(in_3[3:0]));  // open: dot
  ROM #(.addrWidth(9), .dataWidth(32)) rom_1 (.addr({in_5, OREGBUS}), .data(rom_1_data));
  // Probe on OREGBUS
  debounce debounce_1 (.resp(uRESET), .req(RESET_out), .clk(CLK));
  LED led_73 (.in(uRESET));
  hex7seg hex7seg_23 (
    .a(hex7seg_23_a), .b(hex7seg_23_b), .c(hex7seg_23_c), .d(hex7seg_23_d), .e(hex7seg_23_e),
    .f(hex7seg_23_f), .g(hex7seg_23_g), .dp(hex7seg_23_dp), .en(PRGMODE), .value(DBUS[7:4]));  // open: dot
  and and_21 (and_21_out, PRGMODE, nPRGWR);
  and and_22 (and_22_out, PRGMODE, PRGWR);
  _7_Segment_Display u_7_segment_display_27 (
    .g(hex7seg_23_g), .f(hex7seg_23_f), .a(hex7seg_23_a), .b(hex7seg_23_b), .e(hex7seg_23_e),
    .d(hex7seg_23_d), .c(hex7seg_23_c), .dp(hex7seg_23_dp));
  Multiplexer #(.enable("false"), .width(16)) multiplexer_4 (
    .in0(RAMABUS), .in1({in_4, in_3}), .out({abaddrsel, SELABUS}), .sel(PRGMODE));
  or or_1 (selEnRAM, and_21_out, clEnRAM);
  or or_2 (selWRAM, and_22_out, clWRAM);
  or or_3 (or_3_out, and_22_out, CLK);
  or or_4 (ramCLK, or_3_out, cpuCLK);
  D_Flip_Flop d_ff_2 (.D(clDISP), .clk(clDISPLATCH), .Q(d_ff_2_q), .reset(uRESET));  // open: Qn, preset
  assign {s4hs, s4ls, s3hs, s3ls, s2hs, s2ls, s1hs, s1ls} = 1'b1 ? rom_1_data : 32'bz;  // Controlled_Buffer controlled_buffer_29
  hex7seg hex7seg_24 (
    .a(hex7seg_24_a), .b(hex7seg_24_b), .c(hex7seg_24_c), .d(hex7seg_24_d), .e(hex7seg_24_e),
    .f(hex7seg_24_f), .g(hex7seg_24_g), .dp(hex7seg_24_dp), .en(PRGMODE), .value(DBUS[3:0]));  // open: dot
  _7_Segment_Display u_7_segment_display_28 (
    .g(hex7seg_24_g), .f(hex7seg_24_f), .a(hex7seg_24_a), .b(hex7seg_24_b), .e(hex7seg_24_e),
    .d(hex7seg_24_d), .c(hex7seg_24_c), .dp(hex7seg_24_dp));

  // Other names for the same wires on the sheet: Cs = clSPcount; Es = clEnSPREG; Us = clSPcntUp; Sa = clSource;
  //   Xx = clEXX; Ec = clEnCons; clSelConst2 = a2; f2 = a2; Ek = clEnBk4; Lf = clWREGF; E16 = clEnABUSReg;
  //   Lr = clWRAM; Eu = clEnALU; Eb = clEnREGB; Ea = clEnREGA; Ep = clEnPCREG; Cp = clPCcount;
  //   bkrdsel[1:0] = {a1, a0}; clRsel0 = a0; clSelConst0 = a0; f0 = a0; clRsel1 = a1; clSelConst1 = a1; f1 = a1;
  //   clWsel0 = bkwrsel[0]; k0 = bkwrsel[0]; AL8BUS[7:0] = ABUS16[7:0]; AH8BUS[7:0] = ABUS16[15:8];
  //   clWsel1 = bkwrsel[1]; k1 = bkwrsel[1]; contaddr[12:0] = out_6; flagC = fC; FLAGS (some bits) = {flagP, fC};
  //   flagZ = FLAGS[1]; fZ = FLAGS[1]; fP = flagP; flagV = FLAGS[3]; fV = FLAGS[3]; flu0 = FLAGS[4]; fS = FLAGS[4];
  //   flu1 = FLAGS[5]; flu2 = FLAGS[6]; flu3 = FLAGS[7]; OPCODE[7:0] = IREGBUS; PRGADDRESS[15:0] = {in_4, in_3};
  //   PRGDLL4[3:0] = in_3[3:0]; PRGDLH4[3:0] = in_3[7:4]; PRGDHL4[3:0] = in_3[11:8];
  //   PRGDHH4[3:0] = {in_4, in_3[14:12]}; PRGDBUSI[7:0] = DATA_INPUT; PRGDL4[3:0] = DATA_INPUT[3:0];
  //   PRGDH4[3:0] = DATA_INPUT[7:4]; PRGDBUS[7:0] = DBUS; PRGOL4[3:0] = DBUS[3:0]; RAMDBUS[7:0] = DBUS;
  //   PRGOH4[3:0] = DBUS[7:4]; SHAREDABUS[14:0] = SELABUS; ramsel = abaddrsel; SELABUS[15] = abaddrsel; T1 = CONQ[0];
  //   TSTATECON[19:0] = CONQ; T2 = CONQ[1]; T3 = CONQ[2]; T4 = CONQ[3]; T5 = CONQ[4]; T6 = CONQ[5]; T7 = CONQ[6];
  //   T8 = CONQ[7]; T9 = CONQ[8]; T10 = CONQ[9]; T11 = CONQ[10]; T12 = CONQ[11]; T13 = CONQ[12]; T14 = CONQ[13];
  //   T15 = CONQ[14]; T16 = CONQ[15]; T17 = CONQ[16]; T18 = CONQ[17]; T19 = CONQ[18]; T20 = CONQ[19];
  //   WRITEREQ = PRGWR

  // Notes on the sheet:
  //   contents of ROMModule (hex, n*v repeats v):
  //   6c 0 80 52 4f 4d 20 28 43 29 20 4a 6f 68 6e 20 57 69 6c 73 6f 6e 20 32 30 32 31 2e 228*0 6c 6 1 6c b
  //   1 1f 20 23 22 6f e1 e4 e1 6f 28401*0 53 49 4e 0 43 4f 53 0 66 60
  //   JMP 0x8000
  //   'No Action' Control Pins State
  //   Unsued register pins
  //   Diode Matrix
  //   PC REGISTER
  //   SP REGISTER
  //   Source for A Reg Data In
  //   Source for B Reg Data In
  //   16 bit Support for transferring from 8-bit DBUS to ABUS
  //   (set by 'Sa' control line pin)
  //   read select bits shared with Jump select bits
  //   CONTROL MODULE
  //   SAP2 - 'Microprocessor' 
  //   Johnny Wilson - Brighton 2021
  //   Loosely based on the SAP2 microprocessor from the book 'Digital Computer Electronics - An introduction to Microcomputers'  Albert Paul Malvino  1983
  //   ** After loading a program in the 'RAM MODULE' go to the 'DISPLAY MODULE' below to watch the CPU running **
  //   Source For A and B Regs can change from DBUS or 8-bits of the address bus
  //   Example: Load 'simpleprog' into RAM before resetting the circuit.
  //   DISPLAY MODULE
  //   ADD
  //   f0,f1 Jmp cond or bank  sel bits
  //   MAIN 16-BIT REGISTERS
  //   Reg attached directly to RAM address lines
  //   MAIN 8-BIT REGISTERS
  //   ALU UNIT 
  //   A REGISTER
  //   B  REGISTER
  //   SUB
  //   SHIFT LEFT
  //   load flag
  //   RAM MODULE
  //   ALU FUNCTION
  //   SHIFT RIGHT
  //   Bank Reg Possibly share with JMP condition sel bits?
  //   RAM Module Starts at 0x8000 **DO NOT FORGET TO USE .ORG 0x8000 DIRECTIVE ***
  //   4x 8-BIT REG BANK R3,R2,R1,R0
  //   Instruction  REGISTER
  //   OUTPUT REGISTER (HEX)
  //   AND
  //   OR
  //   dec SP/En SP
  //   Two Banks of 4 Regs - Toggled with EXX opcode
  //   NEW DATA
  //   Memory Mapped IO
  //   XOR
  //   PC 16-BIT
  //   read select bits shared with Jump select bits
  //   NOP
  //   16-bit PC Reg
  //   OUTPUT REGISTER (DECIMAL)
  //   S V P Z C
  //   PROGRAMMER UNIT
  //   included for completeness - I recommend you using the LogiSim GUI to edit the RAM directly!
  //   ADDRESS (16-bit but only 4 bits used on SAP1 original)
  //   ADDRESS INPUT
  //   OUTPUT REGISTER (DECIMAL USING 32-BIT ROM)
  //   Sign bit
  //   JUMP - {f1,f0} 00 JPC, 01 JPNZ, 10 JPNC, 11 JMP (no condition)
  //   original conents
  //   JUMP - {k0,f1,f0} 000 JPC, 001 JPNZ, 010 JPNC, 011 JMP (no condition), 100 JPV, 101 JPZ
  //   contents of rom_1 (hex, n*v repeats v):
  //   7e 12 bc b6 d2 e6 ee 32 fe f6 127e 1212 12bc 12b6 12d2 12e6 12ee 1232 12fe 12f6 bc7e bc12 bcbc bcb6
  //   bcd2 bce6 bcee bc32 bcfe bcf6 b67e b612 b6bc b6b6 b6d2 b6e6 b6ee b632 b6fe b6f6 d27e d212 d2bc d2b6
  //   d2d2 d2e6 d2ee d232 d2fe d2f6 e67e e612 e6bc e6b6 e6d2 e6e6 e6ee e632 e6fe e6f6 ee7e ee12 eebc eeb6
  //   eed2 eee6 eeee ee32 eefe eef6 327e 3212 32bc 32b6 32d2 32e6 32ee 3232 32fe 32f6 fe7e fe12 febc feb6
  //   fed2 fee6 feee fe32 fefe fef6 f67e f612 f6bc f6b6 f6d2 f6e6 f6ee f632 f6fe f6f6 127e7e 127e12 127ebc
  //   127eb6 127ed2 127ee6 127eee 127e32 127efe 127ef6 12127e 121212 1212bc 1212b6 1212d2 1212e6 1212ee
  //   121232 1212fe 1212f6 12bc7e 12bc12 12bcbc 12bcb6 12bcd2 12bce6 12bcee 12bc32 12bcfe 12bcf6 12b67e
  //   12b612 12b6bc 12b6b6 12b6d2 12b6e6 12b6ee 12b632 12b6fe 12b6f6 12d27e 12d212 12d2bc 12d2b6 12d2d2
  //   12d2e6 12d2ee 12d232 12d2fe 12d2f6 12e67e 12e612 12e6bc 12e6b6 12e6d2 12e6e6 12e6ee 12e632 12e6fe
  //   12e6f6 12ee7e 12ee12 12eebc 12eeb6 12eed2 12eee6 12eeee 12ee32 12eefe 12eef6 12327e 123212 1232bc
  //   1232b6 1232d2 1232e6 1232ee 123232 1232fe 1232f6 12fe7e 12fe12 12febc 12feb6 12fed2 12fee6 12feee
  //   12fe32 12fefe 12fef6 12f67e 12f612 12f6bc 12f6b6 12f6d2 12f6e6 12f6ee 12f632 12f6fe 12f6f6 bc7e7e
  //   bc7e12 bc7ebc bc7eb6 bc7ed2 bc7ee6 bc7eee bc7e32 bc7efe bc7ef6 bc127e bc1212 bc12bc bc12b6 bc12d2
  //   bc12e6 bc12ee bc1232 bc12fe bc12f6 bcbc7e bcbc12 bcbcbc bcbcb6 bcbcd2 bcbce6 bcbcee bcbc32 bcbcfe
  //   bcbcf6 bcb67e bcb612 bcb6bc bcb6b6 bcb6d2 bcb6e6 bcb6ee bcb632 bcb6fe bcb6f6 bcd27e bcd212 bcd2bc
  //   bcd2b6 bcd2d2 bcd2e6 bcd2ee bcd232 bcd2fe bcd2f6 bce67e bce612 bce6bc bce6b6 bce6d2 bce6e6 7e 12 bc
  //   b6 d2 e6 ee 32 fe f6 127e 1212 12bc 12b6 12d2 12e6 12ee 1232 12fe 12f6 bc7e bc12 bcbc bcb6 bcd2 bce6
  //   bcee bc32 bcfe bcf6 b67e b612 b6bc b6b6 b6d2 b6e6 b6ee b632 b6fe b6f6 d27e d212 d2bc d2b6 d2d2 d2e6
  //   d2ee d232 d2fe d2f6 e67e e612 e6bc e6b6 e6d2 e6e6 e6ee e632 e6fe e6f6 ee7e ee12 eebc eeb6 eed2 eee6
  //   eeee ee32 eefe eef6 327e 3212 32bc 32b6 32d2 32e6 32ee 3232 32fe 32f6 fe7e fe12 febc feb6 fed2 fee6
  //   feee fe32 fefe fef6 f67e f612 f6bc f6b6 f6d2 f6e6 f6ee f632 f6fe f6f6 127e7e 127e12 127ebc 127eb6
  //   127ed2 127ee6 127eee 127e32 127efe 127ef6 12127e 121212 1212bc 1212b6 1212d2 1212e6 1212ee 121232
  //   1212fe 1212f6 12bc7e 12bc12 12bcbc 12bcb6 12bcd2 12bce6 12bcee 12bc32 8012bcfe 8012bc32 8012bcee
  //   8012bce6 8012bcd2 8012bcb6 8012bcbc 8012bc12 8012bc7e 801212f6 801212fe 80121232 801212ee 801212e6
  //   801212d2 801212b6 801212bc 80121212 8012127e 80127ef6 80127efe 80127e32 80127eee 80127ee6 80127ed2
  //   80127eb6 80127ebc 80127e12 80127e7e 8000f6f6 8000f6fe 8000f632 8000f6ee 8000f6e6 8000f6d2 8000f6b6
  //   8000f6bc 8000f612 8000f67e 8000fef6 8000fefe 8000fe32 8000feee 8000fee6 8000fed2 8000feb6 8000febc
  //   8000fe12 8000fe7e 800032f6 800032fe 80003232 800032ee 800032e6 800032d2 800032b6 800032bc 80003212
  //   8000327e 8000eef6 8000eefe 8000ee32 8000eeee 8000eee6 8000eed2 8000eeb6 8000eebc 8000ee12 8000ee7e
  //   8000e6f6 8000e6fe 8000e632 8000e6ee 8000e6e6 8000e6d2 8000e6b6 8000e6bc 8000e612 8000e67e 8000d2f6
  //   8000d2fe 8000d232 8000d2ee 8000d2e6 8000d2d2 8000d2b6 8000d2bc 8000d212 8000d27e 8000b6f6 8000b6fe
  //   8000b632 8000b6ee 8000b6e6 8000b6d2 8000b6b6 8000b6bc 8000b612 8000b67e 8000bcf6 8000bcfe 8000bc32
  //   8000bcee 8000bce6 8000bcd2 8000bcb6 8000bcbc 8000bc12 8000bc7e 800012f6 800012fe 80001232 800012ee
  //   800012e6 800012d2 800012b6 800012bc 80001212 8000127e 800000f6 800000fe 80000032 800000ee 800000e6
  //   800000d2 800000b6 800000bc 80000012
  //   32-bit ROM for Decimal 7Seg Display Unit
  //   ORIGINAL
  //   Currently unused display latch - so always show display Register contents
endmodule

module stackreg (
  input  reset,
  input  load,
  input  ndwn,
  input  counten,
  input  clk,
  input  [15:0] Din,
  input  pcout,
  output [15:0] dbg,
  output [15:0] Dout
);

  Pull_Resistor #(.pull(1)) pull_resistor_1 (.node(ndwn));
  Counter #(.max('hffff), .width(16)) counter_1 (
    .clr(reset), .load(load), .up(ndwn), .count(counten), .clk(clk), .D(Din), .Q(dbg));  // open: carry
  Pull_Resistor pull_resistor_2 (.node(pcout));
  assign Dout = pcout ? dbg : 16'bz;  // Controlled_Buffer controlled_buffer_1
endmodule

// PC
module pcreg (
  input  reset,
  input  load,
  input  counten,
  input  clk,
  input  [15:0] Din,
  input  pcout,
  output [15:0] dbg,
  output [15:0] Dout
);

  Counter #(.max('hffff), .width(16)) counter_1 (
    .clr(reset), .load(load), .up(1'b1), .count(counten), .clk(clk), .D(Din), .Q(dbg));  // open: carry
  Pull_Resistor pull_resistor_1 (.node(pcout));
  assign Dout = pcout ? dbg : 16'bz;  // Controlled_Buffer controlled_buffer_1
endmodule

module controller (
  input  pause,
  input  clr,
  input  [7:0] opcode,
  output [19:0] Q,
  output [12:0] addr,
  output [31:0] cntrl,
  output [7:0] opdec,
  output cpuCLK,
  output ncpuCLK,
  output CLK,
  output nCLK,
  output clkd2
);

  wire clrnop, clrrng, hltpause, not_3_out, or_1_out, undriven;

  or or_1 (or_1_out, hltpause, pause);
  cpuclock cpuclock_1 (.clk(CLK), .clk2(clkd2), .cpuclk(cpuCLK), .pause(or_1_out), .step(undriven));
  assign addr[4:0] = Q[0] ? {5{1'b0}} : 5'bz;  // Controlled_Buffer controlled_buffer_1
  assign addr[4:0] = Q[1] ? 5'b00001 : 5'bz;  // Controlled_Buffer controlled_buffer_2
  assign addr[4:0] = Q[2] ? 5'b00010 : 5'bz;  // Controlled_Buffer controlled_buffer_3
  assign addr[4:0] = Q[3] ? 5'b00011 : 5'bz;  // Controlled_Buffer controlled_buffer_4
  assign addr[4:0] = Q[4] ? 5'b00100 : 5'bz;  // Controlled_Buffer controlled_buffer_5
  assign addr[4:0] = Q[5] ? 5'b00101 : 5'bz;  // Controlled_Buffer controlled_buffer_6
  assign addr[4:0] = Q[6] ? 5'b00110 : 5'bz;  // Controlled_Buffer controlled_buffer_7
  assign addr[4:0] = Q[7] ? 5'b00111 : 5'bz;  // Controlled_Buffer controlled_buffer_8
  assign addr[4:0] = Q[8] ? 5'b01000 : 5'bz;  // Controlled_Buffer controlled_buffer_9
  assign addr[4:0] = Q[9] ? 5'b01001 : 5'bz;  // Controlled_Buffer controlled_buffer_10
  assign addr[4:0] = Q[10] ? 5'b01010 : 5'bz;  // Controlled_Buffer controlled_buffer_11
  assign addr[4:0] = Q[11] ? 5'b01011 : 5'bz;  // Controlled_Buffer controlled_buffer_12
  assign addr[4:0] = Q[12] ? 5'b01100 : 5'bz;  // Controlled_Buffer controlled_buffer_13
  assign addr[4:0] = Q[13] ? 5'b01101 : 5'bz;  // Controlled_Buffer controlled_buffer_14
  assign addr[4:0] = Q[14] ? 5'b01110 : 5'bz;  // Controlled_Buffer controlled_buffer_15
  assign addr[4:0] = Q[15] ? 5'b01111 : 5'bz;  // Controlled_Buffer controlled_buffer_16
  assign addr[4:0] = Q[16] ? 5'b10000 : 5'bz;  // Controlled_Buffer controlled_buffer_17
  assign addr[4:0] = Q[17] ? 5'b10001 : 5'bz;  // Controlled_Buffer controlled_buffer_18
  assign addr[4:0] = Q[18] ? 5'b10010 : 5'bz;  // Controlled_Buffer controlled_buffer_19
  assign addr[4:0] = Q[19] ? 5'b10011 : 5'bz;  // Controlled_Buffer controlled_buffer_20
  assign addr[4:0] = 1'b0 ? 5'b10100 : 5'bz;  // Controlled_Buffer controlled_buffer_21
  not not_1 (nCLK, CLK);
  not not_2 (ncpuCLK, cpuCLK);
  not not_3 (not_3_out, cpuCLK);
  ROM #(.addrWidth(13), .dataWidth(32)) rom_1 (.addr({opcode, addr[4:0]}), .data(cntrl));
  ring20 ring20_1 (.Q(Q), .clr(clrrng), .clk(not_3_out));
  Pull_Resistor pull_resistor_1 (.node(clrnop));
  Comparator #(.width(32)) comparator_1 (.a(cntrl), .b(32'h3e30c401), .eq(clrnop));  // open: gt, lt
  or or_2 (clrrng, clr, clrnop);
  and and_1 (hltpause, opcode[0], opcode[1], opcode[2], opcode[3], opcode[4], opcode[5], opcode[6], opcode[7]);

  assign addr[12:5] = opcode;
  assign opdec = opcode;

  // Other names for the same wires on the sheet: control[31:0] = cntrl; cpuCLKdiv2 = clkd2; Qd[4:0] = addr[4:0];
  //   xpause = pause

  // Notes on the sheet:
  //   Qd is Log2(Q) * 1
  //   This Log2 'table' could be wired as a diode matrix rather than using tristate buffers
  //   contents of rom_1 (hex, n*v repeats v):
  //   5e30c401 be30c401 2630c401 29*3e30c401 5e30c401 be30c401 2630c401 3c10c441 3e70d401 27*3e30c401
  //   5e30c401 be30c401 2630c401 3c13c4c1 3e70d401 27*3e30c401 5e30c401 be30c401 2630c401 5e30c401
  //   ae304401 5e30c401 ae308401 1e30e401 2e10c401 3c70d401 22*3e30c401 5e30c401 be30c401 2630c401
  //   5e30c401 ae304401 5e30c401 ae308401 1e30e401 2e10c401 3c71d401 22*3e30c401 5e30c401 be30c401
  //   2630c401 5e30c401 ae304401 5e30c401 ae308401 3e37e401 24*3e30c401 5e30c401 be30c401 2630c401
  //   5e30c401 ae304401 5e30c401 ae308401 3e35e401 24*3e30c401 5e30c401 be30c401 2630c401 5e30c401
  //   ac30c401 27*3e30c401 5e30c401 be30c401 2630c401 5e30c401 ae10c401 3c71d401 26*3e30c401 5e30c401
  //   be30c401 2630c401 3f20c401 28*3e30c401 5e30c401 be30c401 2630c401 5e30c401 ae304401 5e30c401
  //   ae308401 1e30e401 2c30c401 23*3e30c401 5e30c401 be30c401 2630c401 5e30c401 ae304401 5e30c401
  //   ae308401 1e30e401 3f38c401 23*3e30c401 5e30c401 be30c401 2630c401 29*3e30c401 5e30c401 be30c401
  //   2630c401 29*3e30c401 5e30c401 be30c401 2630c401 29*3e30c401 5e30c401 be30c401 2630c401 29*3e30c401
  //   5e30c401 be30c401 2630c401 3e20cc01 28*3e30c401 5e30c401 be30c401 2630c401 3e21cc01 28*3e30c401
  //   5e30c401 be30c401 2630c401 3e22cc01 28*3e30c401 5e30c401 be30c401 2630c401 3e23cc01 28*3e30c401
  //   5e30c401 be30c401 2630c401 5e30c401 ae304401 5e30c401 ae308401 1e30e401 2e30c001 23*3e30c401
  //   5e30c401 be30c401 2630c401 5e30c401 ae304401 5e30c401 ae308401 1e30e401 2e30c101 23*3e30c401
  //   5e30c401 be30c401 2630c401 5e30c401 ae304401 5e30c401 ae308401 1e30e401 2e30c201 23*3e30c401
  //   5e30c401 be30c401 2630c401 5e30c401 ae304401 5e30c401 ae308401 1e30e401 2e30c301 23*3e30c401
  //   5e30c401 be30c401 2630c401 5e30c401 ae304401 5e30c401 ae308401 1e30e401 3e38cc01 23*3e30c401
  //   5e30c401 be30c401 2630c401 5e30c401 ae304401 5e30c401 ae308401 1e30e401 3e39cc01 23*3e30c401
  //   5e30c401 be30c401 2630c401 5e30c401 ae304401 5e30c401 ae308401 1e30e401 3e3acc01 23*3e30c401
  //   5e30c401 be30c401 2630c401 5e30c401 ae304401 5e30c401 ae308401 1e30e401 3e3bcc01 23*3e30c401
  //   5e30c401 be30c401 2630c401 5e30c401 ae304401 5e30c401 ae308401 3e30e400 24*3e30c401 5e30c401
  //   be30c401 2630c401 3e30c40b 28*3e30c401 5e30c401 be30c401 2630c401 3e30c403 28*3e30c401 5e30c401
  //   be30c401 2630c401 3e30c403 1e30c405 3e38cc03 1e30c405 3e39cc01 24*3e30c401 5e30c401 be30c401
  //   2630c401 3e30c403 1e30c405 3e3acc03 1e30c405 3e3bcc01 24*3e30c401 5e30c401 be30c401 2630c401
  //   3c10c415 28*3e30c401 5e30c401 be30c401 2630c401 1e30c405 2e30c101 3e30c40b 1e30c405 2e30c00b
  //   24*3e30c401 5e30c401 be30c401 2630c401 1e30c405 2e30c301 3e30c40b 1e30c405 2e30c20b 24*3e30c401
  //   5e30c401 be30c401 2630c401 29*3e30c401 5e30c401 be30c401 2630c401 3e30c421 28*3e30c401 5e30c401
  //   be30c401 2630c401 29*3e30c401 5e30c401 be30c401 2630c401 29*3e30c401 5e30c401 be30c401 2630c401
  //   5e30c401 ae30c001 5e30c401 ae30c101 25*3e30c401 5e30c401 be30c401 2630c401 29*3e30c401 5e30c401
  //   be30c401 2630c401 5e30c401 ae30c201 5e30c401 ae30c301 25*3e30c401 5e30c401 be30c401 2630c401
  //   29*3e30c401 5e30c401 be30c401 2630c401 29*3e30c401 5e30c401 be30c401 2630c401 29*3e30c401 5e30c401
  //   be30c401 2630c401 29*3e30c401 5e30c401 be30c401 2630c401 29*3e30c401 5e30c401 be30c401 2630c401
  //   29*3e30c401 5e30c401 be30c401 2630c401 29*3e30c401 5e30c401 be30c401 2630c401 3c30cc01 3e12cc01
  //   3e70d081 3c32cc01 3e10cc01 3e70d281 3c30cc01 3e12cc01 3e70d081 20*3e30c401 5e30c401 be30c401
  //   2630c401 29*3e30c401 5e30c401 be30c401 2630c401 29*3e30c401 5e30c401 be30c401 2630c401 29*3e30c401
  //   5e30c401 be30c401 2630c401 29*3e30c401 5e30c401 be30c401 2630c401 3c31cc01 3e13cc01 3e70d181
  //   3c33cc01 3e11cc01 3e70d381 3c31cc01 3e13cc01 3e70d181 20*3e30c401 5e30c401 be30c401 2630c401
  //   29*3e30c401 5e30c401 be30c401 2630c401 29*3e30c401 5e30c401 be30c401 2630c401 29*3e30c401 5e30c401
  //   be30c401 2630c401 29*3e30c401 5e30c401 be30c401 2630c401 29*3e30c401 5e30c401 be30c401 2630c401
  //   29*3e30c401 5e30c401 be30c401 2630c401 29*3e30c401 5e30c401 be30c401 2630c401 29*3e30c401 5e30c401
  //   be30c401 2630c401 5e30c401 ae30c001 27*3e30c401 5e30c401 be30c401 2630c401 5e30c401 ae30c101
  //   27*3e30c401 5e30c401 be30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
  //   Control Sequencer - with Enhanced SAP2 Microcode ROM
  //   This controller uses one 32-bit dBus ROM. Really not practical to build - please see 'controller_8bitroms' circuit. An alternative replacement
  //   Q is the ring State {1,2,4,8,16,32}
  //   ROM data built with buildcontrolrom.py 
  //   SAP1 Microcode ROM - control = opcode*32 + Log2(Q) 
  //   Stop the CPU Clock if our OPCODE is HLT (0xFF)
  //   Save us defining gate arrays of NAND gates
endmodule

module controller_8bitroms (
  input  clr,
  input  [3:0] opcode,
  output [5:0] Q,
  output [6:0] addr,
  output [23:0] cntrl,
  output [3:0] opdec,
  output cpuCLK,
  output ncpuCLK,
  output CLK,
  output nCLK,
  output clkd2
);

  wire clrnop, clrrng, not_3_out, pause, undriven;

  ROM #(.addrWidth(7)) rom_1 (.addr({opcode, addr[2:0]}), .data(cntrl[23:16]));
  ROM #(.addrWidth(7)) rom_2 (.addr({opcode, addr[2:0]}), .data(cntrl[15:8]));
  ROM #(.addrWidth(7)) rom_3 (.addr({opcode, addr[2:0]}), .data(cntrl[7:0]));
  cpuclock cpuclock_1 (.clk(CLK), .clk2(clkd2), .cpuclk(cpuCLK), .pause(pause), .step(undriven));
  not not_1 (nCLK, CLK);
  not not_2 (ncpuCLK, cpuCLK);
  not not_3 (not_3_out, cpuCLK);
  ring6 ring6_1 (.Q(Q), .clr(clrrng), .clk(not_3_out));
  // Probe on cntrl
  and and_1 (pause, opcode[0], opcode[1], opcode[2], opcode[3]);
  Comparator #(.width(24)) comparator_1 (.a(cntrl), .b(24'h3e3000), .eq(clrnop));  // open: gt, lt
  Pull_Resistor pull_resistor_1 (.node(clrnop));
  or or_1 (clrrng, clr, clrnop);
  assign addr[2:0] = Q[0] ? 3'b000 : 3'bz;  // Controlled_Buffer controlled_buffer_1
  assign addr[2:0] = Q[1] ? 3'b001 : 3'bz;  // Controlled_Buffer controlled_buffer_2
  assign addr[2:0] = Q[2] ? 3'b010 : 3'bz;  // Controlled_Buffer controlled_buffer_3
  assign addr[2:0] = Q[3] ? 3'b011 : 3'bz;  // Controlled_Buffer controlled_buffer_4
  assign addr[2:0] = Q[4] ? 3'b100 : 3'bz;  // Controlled_Buffer controlled_buffer_5
  assign addr[2:0] = Q[5] ? 3'b101 : 3'bz;  // Controlled_Buffer controlled_buffer_6

  assign addr[6:3] = opcode;
  assign opdec = opcode;

  // Other names for the same wires on the sheet: Qd[2:0] = addr[2:0]; control[23:0] = cntrl; rom3[7:0] = cntrl[7:0];
  //   rom2[7:0] = cntrl[15:8]; rom1[7:0] = cntrl[23:16]; cpuCLKdiv2 = clkd2

  // Notes on the sheet:
  //   contents of rom_1 (hex, n*v repeats v):
  //   5e be 26 1a 2c 3e 3e 3e 5e be 26 1a 2e 3c 3e 3e 5e be 26 1a 2e 3c 3e 3e 5e be 26 1a 3f 3e 3e 3e 5e
  //   be 26 5*3e 5e be 26 5*3e 5e be 26 5e ac 3e 3e 3e 5e be 26 5e ae 3c 3e 3e 5e be 26 5e ae 3c 3e 3e 5e
  //   be 26 5*3e 5e be 26 5*3e 5e be 26 5*3e 5e be 26 5*3e 5e be 26 5*3e 5e be 26 3f 4*3e 5e be 26 5*3e
  //   contents of rom_2 (hex, n*v repeats v):
  //   12*30 10 70 6*30 10 f0 6*30 38 6*30 37 7*30 35 16*30 10 70 6*30 10 f0 45*30 20 12*30
  //   Top 8-bits
  //   Middle 8-bits
  //   Lower 8-bits
  //   Control Sequencer - with Enhanced SAP 1 Microcode 8-bit ROMs
  //   This controller replaces 'controller.circ' - as this uses 3 lots of 8-bit Data ROMs instead of the old 24-bit Data format
  //   Q is the ring State {1,2,4,8,16,32}
  //   ROM data built with buildcontrolrom.py 
  //   ROM data built with buildcontrolrom.py 
  //   ROM data built with buildcontrolrom.py 
  //   SAP1 Microcode ROM - control = opcode*8 + Log2(Q) 
  //   Stop the CPU Clock if our OPCODE is HLT (0xf)
  //   Save us defining gate arrays of NAND gates
  //   Qd is Log2(Q) * 1
  //   This Log2 'table' could be wired as a diode matrix rather than using tristate buffers
endmodule

module memIOunit (
  input  [7:0] din,
  input  [15:0] addr,
  input  IOWrReq,
  input  IORdReq,
  output [7:0] dout,
  output [3:0] out_6,
  output out_7
);

  wire deviceReq;
  wire [7:0] undriven;

  and and_1 (deviceReq, addr[4], addr[5], addr[6], addr[7], addr[8], addr[9], addr[10], addr[11], addr[12], addr[13], addr[14], ~addr[15]);  // AND_Gate
  and and_2 (out_7, IOWrReq, deviceReq);
  assign dout = 1'b0 ? undriven : 8'bz;  // Controlled_Buffer controlled_buffer_1
  assign out_6 = out_7 ? addr[3:0] : 4'bz;  // Controlled_Buffer controlled_buffer_2

  // Other names for the same wires on the sheet: device[3:0] = addr[3:0]

  // Notes on the sheet:
  //   Look for Writes to 0x7FFFX
  //   IF this happens then present the bottom 4 bits of the address to its output
  //   TO BE IMPLEMENTED - BUT FOR NOW A VERY SIMPLE MEMORY MAPPED DEVICE HANDLER
endmodule

module soundunit (
  input  [7:0] din,
  input  [1:0] sreg,
  input  wr,
  input  reset,
  output [13:0] frq,
  output [3:0] vol,
  output en
);

  wire we0, we1, we2, we3, wr0, wr1, wr2;
  wire [6:4] vole;
  wire [7:6] freqhi;

  Decoder #(.select(2)) decoder_1 (.out0(we0), .out1(we1), .out2(we2), .out3(we3), .sel(sreg));  // open: en
  and and_1 (wr0, wr, we0);
  and and_2 (wr1, wr, we1);
  and and_3 (wr2, wr, we2);
  Register register_1 (.D(din), .clk(wr0), .Q(frq[7:0]), .clr(reset));  // open: en
  Register register_2 (.D(din), .clk(wr1), .Q({freqhi, frq[13:8]}), .clr(reset));  // open: en
  Register register_3 (.D(din), .clk(wr2), .Q({en, vole, vol}), .clr(reset));  // open: en
  // Buzzer #(.vol_width(4)) buzzer_1: pin names not known; wires that end beside it: frq, en, vol

  // Other names for the same wires on the sheet: freq[13:0] = frq; freqlo[7:0] = frq[7:0]; freqhi[5:0] = frq[13:8];
  //   vole (some bits) = {en, vol}
endmodule

module ring20 (
  input  clr,
  input  clk,
  output [19:0] Q
);

  wire q20, q21;

  D_Flip_Flop d_ff_1 (.D(Q[6]), .clk(clk), .Q(Q[7]), .reset(clr));  // open: Qn, preset
  D_Flip_Flop d_ff_2 (.D(Q[13]), .clk(clk), .Q(Q[14]), .reset(clr));  // open: Qn, preset
  D_Flip_Flop d_ff_3 (.D(q20), .clk(clk), .Q(q21), .reset(clr));  // open: Qn, preset
  D_Flip_Flop d_ff_4 (.D(Q[5]), .clk(clk), .Q(Q[6]), .reset(clr));  // open: Qn, preset
  D_Flip_Flop d_ff_5 (.D(Q[12]), .clk(clk), .Q(Q[13]), .reset(clr));  // open: Qn, preset
  D_Flip_Flop d_ff_6 (.D(Q[19]), .clk(clk), .Q(q20), .reset(clr));  // open: Qn, preset
  D_Flip_Flop d_ff_7 (.D(Q[4]), .clk(clk), .Q(Q[5]), .reset(clr));  // open: Qn, preset
  D_Flip_Flop d_ff_8 (.D(Q[11]), .clk(clk), .Q(Q[12]), .reset(clr));  // open: Qn, preset
  D_Flip_Flop d_ff_9 (.D(Q[18]), .clk(clk), .Q(Q[19]), .reset(clr));  // open: Qn, preset
  D_Flip_Flop d_ff_10 (.D(Q[3]), .clk(clk), .Q(Q[4]), .reset(clr));  // open: Qn, preset
  D_Flip_Flop d_ff_11 (.D(Q[10]), .clk(clk), .Q(Q[11]), .reset(clr));  // open: Qn, preset
  D_Flip_Flop d_ff_12 (.D(Q[17]), .clk(clk), .Q(Q[18]), .reset(clr));  // open: Qn, preset
  D_Flip_Flop d_ff_13 (.D(Q[2]), .clk(clk), .Q(Q[3]), .reset(clr));  // open: Qn, preset
  D_Flip_Flop d_ff_14 (.D(Q[16]), .clk(clk), .Q(Q[17]), .reset(clr));  // open: Qn, preset
  D_Flip_Flop d_ff_15 (.D(Q[9]), .clk(clk), .Q(Q[10]), .reset(clr));  // open: Qn, preset
  D_Flip_Flop d_ff_16 (.D(Q[1]), .clk(clk), .Q(Q[2]), .reset(clr));  // open: Qn, preset
  D_Flip_Flop d_ff_17 (.D(Q[8]), .clk(clk), .Q(Q[9]), .reset(clr));  // open: Qn, preset
  D_Flip_Flop d_ff_18 (.D(Q[15]), .clk(clk), .Q(Q[16]), .reset(clr));  // open: Qn, preset
  D_Flip_Flop d_ff_19 (.D(Q[0]), .clk(clk), .Q(Q[1]), .reset(clr));  // open: Qn, preset
  D_Flip_Flop d_ff_20 (.D(Q[7]), .clk(clk), .Q(Q[8]), .reset(clr));  // open: Qn, preset
  D_Flip_Flop d_ff_21 (.D(Q[14]), .clk(clk), .Q(Q[15]), .reset(clr));  // open: Qn, preset
  D_Flip_Flop d_ff_22 (.D(Q[19]), .clk(clk), .Q(Q[0]), .preset(clr));  // open: Qn, reset
endmodule

module ring4 (
  input  clr,
  input  clk,
  output [3:0] Q
);

  wire q4, q5, q6, q7;

  D_Flip_Flop d_ff_1 (.D(q6), .clk(clk), .Q(q7), .reset(clr));  // open: Qn, preset
  D_Flip_Flop d_ff_2 (.D(q5), .clk(clk), .Q(q6), .reset(clr));  // open: Qn, preset
  D_Flip_Flop d_ff_3 (.D(q4), .clk(clk), .Q(q5), .reset(clr));  // open: Qn, preset
  D_Flip_Flop d_ff_4 (.D(Q[3]), .clk(clk), .Q(q4), .reset(clr));  // open: Qn, preset
  D_Flip_Flop d_ff_5 (.D(Q[2]), .clk(clk), .Q(Q[3]), .reset(clr));  // open: Qn, preset
  D_Flip_Flop d_ff_6 (.D(Q[1]), .clk(clk), .Q(Q[2]), .reset(clr));  // open: Qn, preset
  D_Flip_Flop d_ff_7 (.D(Q[0]), .clk(clk), .Q(Q[1]), .reset(clr));  // open: Qn, preset
  D_Flip_Flop d_ff_8 (.D(Q[3]), .clk(clk), .Q(Q[0]), .preset(clr));  // open: Qn, reset
endmodule

module cpuclock (
  input  pause,
  input  step,
  output clk,
  output cpuclk,
  output clk2
);

  wire and_1_out, and_2_out, d_ff_1_qn, not_1_out;

  Clock clock_1 (.out(clk));
  D_Flip_Flop d_ff_1 (.D(d_ff_1_qn), .clk(clk), .Q(clk2), .Qn(d_ff_1_qn));  // open: preset, reset
  not not_1 (not_1_out, pause);
  and and_1 (and_1_out, clk, not_1_out);
  and and_2 (and_2_out, pause, step);
  or or_1 (cpuclk, and_1_out, and_2_out);

  // Other names for the same wires on the sheet: cpuCLKdiv2 = clk2; MAINCLK = clk
endmodule

module segdecdisplay (
  input  reset,
  input  clk,
  input  [7:0] value,
  input  sign,
  input  en,
  output [3:0] anode,
  output [7:0] hseg
);

  wire wclk;
  wire [3:0] register_1_q, ring4_1_q;
  wire [7:0] register_2_q, SEGROM_data;

  not not_1 (wclk, clk);
  ROM #(.addrWidth(13)) SEGROM (.addr({1'b0, ring4_1_q, value}), .data(SEGROM_data));
  ring4 ring4_1 (.Q(ring4_1_q), .clr(reset), .clk(clk));
  Register #(.width(4)) register_1 (.D(ring4_1_q), .en(en), .clk(wclk), .Q(register_1_q));  // open: clr
  Register register_2 (.D(SEGROM_data), .en(en), .clk(wclk), .Q(register_2_q));  // open: clr
  assign anode = en ? register_1_q : 4'bz;  // Controlled_Buffer controlled_buffer_1
  assign hseg = en ? register_2_q : 8'bz;  // Controlled_Buffer controlled_buffer_2

  // Other names for the same wires on the sheet: clr = reset; sgn = sign

  // Notes on the sheet:
  //   contents of SEGROM (hex, n*v repeats v):
  //   256*0 7e 12 bc b6 d2 e6 ee 32 fe f2 7e 12 bc b6 d2 e6 ee 32 fe f2 7e 12 bc b6 d2 e6 ee 32 fe f2 7e
  //   12 bc b6 d2 e6 ee 32 fe f2 7e 12 bc b6 d2 e6 ee 32 fe f2 7e 12 bc b6 d2 e6 ee 32 fe f2 7e 12 bc b6
  //   d2 e6 ee 32 fe f2 7e 12 bc b6 d2 e6 ee 32 fe f2 7e 12 bc b6 d2 e6 ee 32 fe f2 7e 12 bc b6 d2 e6 ee
  //   32 fe f2 7e 12 bc b6 d2 e6 ee 32 fe f2 7e 12 bc b6 d2 e6 ee 32 fe f2 7e 12 bc b6 d2 e6 ee 32 fe f2
  //   7e 12 bc b6 d2 e6 ee 32 fe f2 7e 12 bc b6 d2 e6 ee 32 fe f2 7e 12 bc b6 d2 e6 ee 32 fe f2 7e 12 bc
  //   b6 d2 e6 ee 32 fe f2 7e 12 bc b6 d2 e6 ee 32 fe f2 7e 12 bc b6 d2 e6 ee 32 fe f2 7e 12 bc b6 d2 e6
  //   ee 32 fe f2 7e 12 bc b6 d2 e6 ee 32 fe f2 7e 12 bc b6 d2 e6 ee 32 fe f2 7e 12 bc b6 d2 e6 ee 32 fe
  //   f2 7e 12 bc b6 d2 e6 ee 32 fe f2 7e 12 bc b6 d2 e6 ee 32 fe f2 7e 12 bc b6 d2 e6 10*0 10*12 10*bc
  //   10*b6 10*d2 10*e6 10*ee 10*32 10*fe 10*f2 10*7e 10*12 10*bc 10*b6 10*d2 10*e6 10*ee 10*32 10*fe
  //   10*f2 10*7e 10*12 10*bc 10*b6 10*d2 6*e6 6*1 10*ff 340*0 100*12 56*bc
endmodule

module debounce (
  input  req,
  input  clk,
  output resp
);

  wire d_ff_1_q, d_ff_1_qn, d_ff_2_qn;

  D_Flip_Flop d_ff_1 (.D(req), .clk(clk), .Q(d_ff_1_q), .Qn(d_ff_1_qn));  // open: preset, reset
  D_Flip_Flop d_ff_2 (.D(d_ff_1_q), .clk(clk), .Qn(d_ff_2_qn));  // open: Q, preset, reset
  D_Flip_Flop d_ff_3 (.D(d_ff_2_qn), .clk(clk), .Qn(resp));  // open: Q, preset, reset
endmodule

module toggleswitch (
  input  I,
  input  clk,
  input  res,
  output switch,
  output latch
);

  wire d_ff_1_q, d_ff_2_qn;

  D_Flip_Flop d_ff_1 (.D(I), .clk(clk), .Q(d_ff_1_q), .reset(res));  // open: Qn, preset
  D_Flip_Flop d_ff_2 (.D(d_ff_2_qn), .clk(d_ff_1_q), .Q(switch), .Qn(d_ff_2_qn), .reset(res));  // open: preset
  D_Flip_Flop d_ff_3 (.D(d_ff_1_q), .clk(clk), .Q(latch), .reset(res));  // open: Qn, preset
endmodule

// ALU
module alu (
  input  cin,
  input  [7:0] A,
  input  [7:0] B,
  input  en,
  input  [5:0] fn,
  output [7:0] res,
  output C,
  output Z,
  output P,
  output V,
  output S
);

  wire and_2_out, and_3_out, and_4_out, and_5_out, and_6_out, cia, coa, cos, cOUT, cpo, not_1_out, not_2_out,
       not_3_out, not_4_out, not_shift, Subtract_Function;
  wire [4:1] aluflags_z;
  wire [7:0] aunit_s, lunit_res, sunit_res;

  not not_1 (not_1_out, fn[2]);
  not not_2 (not_2_out, fn[3]);
  shiftunit sunit (.res(sunit_res), .cout(cos), .A(A), .sfn(fn[5:4]), .cin(cin));
  logicunit lunit (.Res(lunit_res), .B(B), .A(A), .lfnc(fn[3:0]));
  xnor xnor_1 (not_shift, fn[4], fn[5]);
  and and_1 (Subtract_Function, fn[0], fn[1], not_1_out, not_2_out);
  adderunit aunit (.cout(coa), .S(aunit_s), .B(lunit_res), .A(sunit_res), .cin(cia));
  alures aluflags (
    .V(aluflags_z[3]), .P(aluflags_z[2]), .S(aluflags_z[4]), .Z(aluflags_z[1]), .aMSB(A[7]), .bMSB(B[7]),
    .ares(aunit_s));
  assign res = en ? aunit_s : 8'bz;  // Controlled_Buffer controlled_buffer_1
  assign {S, V, P, Z, C} = en ? {aluflags_z, cOUT} : 5'bz;  // Controlled_Buffer controlled_buffer_2
  and and_2 (and_2_out, not_shift, coa);
  or or_1 (cpo, and_2_out, and_3_out);
  not not_3 (not_3_out, not_shift);
  and and_3 (and_3_out, not_3_out, cos);
  or or_2 (cOUT, and_5_out, and_6_out);
  and and_4 (and_4_out, cos, not_shift);
  and and_5 (and_5_out, Subtract_Function, cin);
  and and_6 (and_6_out, not_4_out, cpo);
  or or_3 (cia, Subtract_Function, and_4_out);
  not not_4 (not_4_out, Subtract_Function);

  // Other names for the same wires on the sheet: aMSB = A[7]; bMSB = B[7]; enable = en; f0 = fn[0];
  //   lfn[3:0] = fn[3:0]; f1 = fn[1]; f2 = fn[2]; f3 = fn[3]; f4 = fn[4]; sfn[1:0] = fn[5:4]; f5 = fn[5]

  // Notes on the sheet:
  //   Valid functions fn
  //   ADD 001100
  //   SUB  000011
  //   AND  111000
  //   OR   111110
  //   XOR  110110
  //   SHR  010000
  //   SHL  100000
  //   0xc
  //   0x3
  //   0x38
  //   0x3e
  //   0x36
  //   0x10
  //   0x20
  //   The 'NOT B' logic function is used for 'Subtract'
  //   We need to set Carry if this is the case
  //   If we are executing SHR or SHL we need to ignore carry results from ADDER unit
  //   IF 'subtracting' output original carry in
endmodule

module adderunit (
  input  [7:0] A,
  input  [7:0] B,
  input  cin,
  output cout,
  output [7:0] S
);

  wire c0, c1, c2, c3, c4, c5, c6;

  fulladder fulladder_1 (.S(S[0]), .Co(c0), .A(A[0]), .B(B[0]), .Ci(cin));
  fulladder fulladder_2 (.S(S[1]), .Co(c1), .A(A[1]), .B(B[1]), .Ci(c0));
  fulladder fulladder_3 (.S(S[2]), .Co(c2), .A(A[2]), .B(B[2]), .Ci(c1));
  fulladder fulladder_4 (.S(S[3]), .Co(c3), .A(A[3]), .B(B[3]), .Ci(c2));
  fulladder fulladder_5 (.S(S[4]), .Co(c4), .A(A[4]), .B(B[4]), .Ci(c3));
  fulladder fulladder_6 (.S(S[5]), .Co(c5), .A(A[5]), .B(B[5]), .Ci(c4));
  fulladder fulladder_7 (.S(S[6]), .Co(c6), .A(A[6]), .B(B[6]), .Ci(c5));
  fulladder fulladder_8 (.S(S[7]), .Co(cout), .A(A[7]), .B(B[7]), .Ci(c6));

  // Other names for the same wires on the sheet: c7 = cout

  // Notes on the sheet:
  //   8-Bit Adder with Carry In
endmodule

module logicunit (
  input  [7:0] B,
  input  [7:0] A,
  input  [3:0] lfnc,
  output [7:0] Res
);

  wire en;

  Multiplexer #(.select(2)) multiplexer_1 (
    .in0(lfnc[0]), .in1(lfnc[1]), .in2(lfnc[2]), .in3(lfnc[3]), .out(Res[0]), .sel({B[0], A[0]}), .en(en));
  Multiplexer #(.select(2)) multiplexer_2 (
    .in0(lfnc[0]), .in1(lfnc[1]), .in2(lfnc[2]), .in3(lfnc[3]), .out(Res[1]), .sel({B[1], A[1]}), .en(en));
  Multiplexer #(.select(2)) multiplexer_3 (
    .in0(lfnc[0]), .in1(lfnc[1]), .in2(lfnc[2]), .in3(lfnc[3]), .out(Res[2]), .sel({B[2], A[2]}), .en(en));
  Multiplexer #(.select(2)) multiplexer_4 (
    .in0(lfnc[0]), .in1(lfnc[1]), .in2(lfnc[2]), .in3(lfnc[3]), .out(Res[3]), .sel({B[3], A[3]}), .en(en));
  Multiplexer #(.select(2)) multiplexer_5 (
    .in0(lfnc[0]), .in1(lfnc[1]), .in2(lfnc[2]), .in3(lfnc[3]), .out(Res[4]), .sel({B[4], A[4]}), .en(en));
  Multiplexer #(.select(2)) multiplexer_6 (
    .in0(lfnc[0]), .in1(lfnc[1]), .in2(lfnc[2]), .in3(lfnc[3]), .out(Res[5]), .sel({B[5], A[5]}), .en(en));
  Multiplexer #(.select(2)) multiplexer_7 (
    .in0(lfnc[0]), .in1(lfnc[1]), .in2(lfnc[2]), .in3(lfnc[3]), .out(Res[6]), .sel({B[6], A[6]}), .en(en));
  Multiplexer #(.select(2)) multiplexer_8 (
    .in0(lfnc[0]), .in1(lfnc[1]), .in2(lfnc[2]), .in3(lfnc[3]), .out(Res[7]), .sel({B[7], A[7]}), .en(en));

  // Other names for the same wires on the sheet: fnc[3:0] = lfnc; r0 = Res[0]; r1 = Res[1]; r2 = Res[2]; r3 = Res[3];
  //   r4 = Res[4]; r5 = Res[5]; r6 = Res[6]; r7 = Res[7]

  // Notes on the sheet:
  //   LOGIC Units Made out of MUXes
  //   0xa          A
  //   0xc          B
  //   0x8          AND
  //   0xe          OR
  //   0x6          XOR
  //   0x1          NOR
  //   0xf          255
  //   lfnc         Logic Function
  //   0x7          NAND
  //   0x3          NOT B
  //   0x5          NOT A
  //   0x0         Zero (0)
endmodule

module shiftunit (
  input  [7:0] A,
  input  [1:0] sfn,
  input  cin,
  output [7:0] res,
  output cout
);

  wire en;

  Multiplexer #(.select(2)) multiplexer_1 (
    .in0(A[0]), .in1(A[1]), .in2(cin), .in3(1'b0), .out(res[0]), .sel(sfn), .en(en));
  Multiplexer #(.select(2)) multiplexer_2 (
    .in0(A[4]), .in1(A[5]), .in2(A[3]), .in3(1'b0), .out(res[4]), .sel(sfn), .en(en));
  Multiplexer #(.select(2)) multiplexer_3 (
    .in0(A[1]), .in1(A[2]), .in2(A[0]), .in3(1'b0), .out(res[1]), .sel(sfn), .en(en));
  Multiplexer #(.select(2)) multiplexer_4 (
    .in0(A[5]), .in1(A[6]), .in2(A[4]), .in3(1'b0), .out(res[5]), .sel(sfn), .en(en));
  Multiplexer #(.select(2)) multiplexer_5 (
    .in0(cin), .in1(A[0]), .in2(A[7]), .in3(1'b0), .out(cout), .sel(sfn), .en(en));
  Multiplexer #(.select(2)) multiplexer_6 (
    .in0(A[2]), .in1(A[3]), .in2(A[1]), .in3(1'b0), .out(res[2]), .sel(sfn), .en(en));
  Multiplexer #(.select(2)) multiplexer_7 (
    .in0(A[6]), .in1(A[7]), .in2(A[5]), .in3(1'b0), .out(res[6]), .sel(sfn), .en(en));
  Multiplexer #(.select(2)) multiplexer_8 (
    .in0(A[3]), .in1(A[4]), .in2(A[2]), .in3(1'b0), .out(res[3]), .sel(sfn), .en(en));
  Multiplexer #(.select(2)) multiplexer_9 (
    .in0(A[7]), .in1(cin), .in2(A[6]), .in3(1'b0), .out(res[7]), .sel(sfn), .en(en));

  // Other names for the same wires on the sheet: r0 = res[0]; r1 = res[1]; r2 = res[2]; r3 = res[3]; r4 = res[4];
  //   r5 = res[5]; r6 = res[6]; r7 = res[7]; sfnc[1:0] = sfn

  // Notes on the sheet:
  //   sfnc         Shift Function
  //   b00          no change
  //   b01          Shift Right
  //   b10          Shift Left
  //   b11          Clear
endmodule

module fulladder (
  input  A,
  input  B,
  input  Ci,
  output S,
  output Co
);

  wire and_1_out, and_2_out, and_3_out, or_1_out, xor_1_out;

  xor xor_1 (xor_1_out, A, B);
  and and_1 (and_1_out, A, B);
  and and_2 (and_2_out, A, Ci);
  and and_3 (and_3_out, B, Ci);
  or or_1 (or_1_out, and_1_out, and_2_out);
  xor xor_2 (S, xor_1_out, Ci);
  or or_2 (Co, or_1_out, and_3_out);

  // Notes on the sheet:
  //   Full 1-bit Adder (carry In, A, B) --> (S(um), carry out)
endmodule

module alures (
  input  [7:0] ares,
  input  aMSB,
  input  bMSB,
  output Z,
  output S,
  output P,
  output V
);

  wire or_1_out, or_2_out, or_3_out, or_4_out, or_5_out, or_6_out, xor_1_out, xor_2_out, xor_3_out,
       xor_4_out, xor_5_out, xor_6_out, xor_7_out, xor_8_out;

  xor xor_1 (xor_1_out, aMSB, ares[7]);
  xor xor_2 (xor_2_out, ares[7], bMSB);
  and and_1 (V, xor_1_out, xor_2_out);
  or or_1 (or_1_out, ares[7], ares[6]);
  or or_2 (or_2_out, ares[5], ares[4]);
  or or_3 (or_3_out, ares[3], ares[2]);
  or or_4 (or_4_out, ares[1], ares[0]);
  xor xor_3 (xor_3_out, ares[7], ares[6]);
  xor xor_4 (xor_4_out, ares[5], ares[4]);
  xor xor_5 (xor_5_out, ares[3], ares[2]);
  xor xor_6 (xor_6_out, ares[1], ares[0]);
  or or_5 (or_5_out, or_1_out, or_2_out);
  or or_6 (or_6_out, or_3_out, or_4_out);
  xor xor_7 (xor_7_out, xor_3_out, xor_4_out);
  xor xor_8 (xor_8_out, xor_5_out, xor_6_out);
  nor nor_1 (Z, or_5_out, or_6_out);
  xor xor_9 (P, xor_7_out, xor_8_out);

  assign S = ares[7];

  // Other names for the same wires on the sheet: r0 = ares[0]; r1 = ares[1]; r2 = ares[2]; r3 = ares[3]; r4 = ares[4];
  //   r5 = ares[5]; r6 = ares[6]; r7 = ares[7]; Overflow = V; ParityOdd = P; Zero = Z
endmodule

module ring6 (
  input  clr,
  input  clk,
  output [5:0] Q
);

  wire q6, q7;

  D_Flip_Flop d_ff_1 (.D(q6), .clk(clk), .Q(q7), .reset(clr));  // open: Qn, preset
  D_Flip_Flop d_ff_2 (.D(Q[5]), .clk(clk), .Q(q6), .reset(clr));  // open: Qn, preset
  D_Flip_Flop d_ff_3 (.D(Q[4]), .clk(clk), .Q(Q[5]), .reset(clr));  // open: Qn, preset
  D_Flip_Flop d_ff_4 (.D(Q[3]), .clk(clk), .Q(Q[4]), .reset(clr));  // open: Qn, preset
  D_Flip_Flop d_ff_5 (.D(Q[2]), .clk(clk), .Q(Q[3]), .reset(clr));  // open: Qn, preset
  D_Flip_Flop d_ff_6 (.D(Q[1]), .clk(clk), .Q(Q[2]), .reset(clr));  // open: Qn, preset
  D_Flip_Flop d_ff_7 (.D(Q[0]), .clk(clk), .Q(Q[1]), .reset(clr));  // open: Qn, preset
  D_Flip_Flop d_ff_8 (.D(Q[5]), .clk(clk), .Q(Q[0]), .preset(clr));  // open: Qn, reset
endmodule

// PC-4bit
module pcreg4 (
  input  reset,
  input  load,
  input  counten,
  input  clk,
  input  [15:0] Din,
  input  pcout,
  output [15:0] dbg,
  output [15:0] Dout
);

  Counter #(.max('hf), .width(4)) counter_1 (
    .clr(reset), .load(load), .up(1'b1), .count(counten), .clk(clk), .D(Din[3:0]), .Q(dbg[3:0]));  // open: carry
  Bit_Extender #(.in_width(4), .\type ("zero")) bit_extender_1 ();  // open: in, out
  assign Dout = pcout ? {{12{1'b0}}, dbg[3:0]} : 16'bz;  // Controlled_Buffer controlled_buffer_1
  Pull_Resistor pull_resistor_1 (.node(pcout));

  assign dbg[15:4] = {12{1'b0}};
endmodule

module reg8bank (
  input  clk,
  input  [7:0] I,
  input  [2:0] regsel,
  input  [7:0] weMask,
  input  res,
  input  en,
  output [7:0] Q
);

  wire en0, en1, en2, en3, en4, en5, en6, en7, we5;
  wire [7:0] bankout, register_1_q, register_2_q, register_3_q, register_4_q, register_5_q, register_6_q,
       register_7_q, register_8_q;

  Decoder #(.select(3)) decoder_1 (
    .out0(en0), .out1(en1), .out2(en2), .out3(en3), .out4(en4), .out5(en5), .out6(en6), .out7(en7),
    .sel(regsel));  // open: en
  Register register_1 (.D(I), .en(weMask[0]), .clk(clk), .Q(register_1_q), .clr(res));
  Pull_Resistor pull_resistor_1 (.node(en0));
  Register register_2 (.D(I), .en(weMask[2]), .clk(clk), .Q(register_2_q), .clr(res));
  Register register_3 (.D(I), .en(weMask[5]), .clk(clk), .Q(register_3_q), .clr(res));
  Register register_4 (.D(I), .en(weMask[6]), .clk(clk), .Q(register_4_q), .clr(res));
  assign bankout = en0 ? register_1_q : 8'bz;  // Controlled_Buffer controlled_buffer_1
  assign bankout = en2 ? register_2_q : 8'bz;  // Controlled_Buffer controlled_buffer_2
  Pull_Resistor pull_resistor_2 (.node(en2));
  assign bankout = en4 ? register_3_q : 8'bz;  // Controlled_Buffer controlled_buffer_3
  Pull_Resistor pull_resistor_3 (.node(en4));
  assign bankout = en6 ? register_4_q : 8'bz;  // Controlled_Buffer controlled_buffer_4
  Pull_Resistor pull_resistor_4 (.node(en6));
  Register register_5 (.D(I), .en(weMask[1]), .clk(clk), .Q(register_5_q), .clr(res));
  Register register_6 (.D(I), .en(weMask[3]), .clk(clk), .Q(register_6_q), .clr(res));
  Register register_7 (.D(I), .en(we5), .clk(clk), .Q(register_7_q), .clr(res));
  Register register_8 (.D(I), .en(weMask[7]), .clk(clk), .Q(register_8_q), .clr(res));
  assign bankout = en1 ? register_5_q : 8'bz;  // Controlled_Buffer controlled_buffer_5
  Pull_Resistor pull_resistor_5 (.node(en1));
  assign bankout = en3 ? register_6_q : 8'bz;  // Controlled_Buffer controlled_buffer_6
  Pull_Resistor pull_resistor_6 (.node(en3));
  assign bankout = en5 ? register_7_q : 8'bz;  // Controlled_Buffer controlled_buffer_7
  Pull_Resistor pull_resistor_7 (.node(en5));
  assign bankout = en7 ? register_8_q : 8'bz;  // Controlled_Buffer controlled_buffer_8
  Pull_Resistor pull_resistor_8 (.node(en7));
  assign Q = en ? bankout : 8'bz;  // Controlled_Buffer controlled_buffer_9
  Pull_Resistor pull_resistor_9 (.node(en));

  assign weMask[4] = weMask[5];

  // Other names for the same wires on the sheet: dataIn[7:0] = I; reset = res; selreg[2:0] = regsel; we0 = weMask[0];
  //   we1 = weMask[1]; we2 = weMask[2]; we3 = weMask[3]; we4 = weMask[5]; we6 = weMask[6]; we7 = weMask[7]

  // Notes on the sheet:
  //   8 Bank 8-bit Registers multi select on writing
endmodule

module reg4bank (
  input  clk,
  input  [7:0] I,
  input  [1:0] regsel,
  input  we,
  input  [1:0] wesel,
  input  res,
  input  en,
  output [7:0] Q,
  output [31:0] out_9
);

  wire en0, en1, en2, en3, we0, we1, we2, we3;
  wire [7:0] bankout;

  Decoder #(.select(2)) decoder_1 (.out0(en0), .out1(en1), .out2(en2), .out3(en3), .sel(regsel));  // open: en
  Decoder #(.select(2)) decoder_2 (.out0(we0), .out1(we1), .out2(we2), .out3(we3), .sel(wesel), .en(we));
  Register register_1 (.D(I), .en(we0), .clk(clk), .Q(out_9[7:0]), .clr(res));
  Pull_Resistor pull_resistor_1 (.node(en0));
  Register register_2 (.D(I), .en(we2), .clk(clk), .Q(out_9[23:16]), .clr(res));
  assign bankout = en0 ? out_9[7:0] : 8'bz;  // Controlled_Buffer controlled_buffer_1
  assign bankout = en2 ? out_9[23:16] : 8'bz;  // Controlled_Buffer controlled_buffer_2
  Pull_Resistor pull_resistor_2 (.node(en2));
  Register register_3 (.D(I), .en(we1), .clk(clk), .Q(out_9[15:8]), .clr(res));
  Register register_4 (.D(I), .en(we3), .clk(clk), .Q(out_9[31:24]), .clr(res));
  assign bankout = en1 ? out_9[15:8] : 8'bz;  // Controlled_Buffer controlled_buffer_3
  Pull_Resistor pull_resistor_3 (.node(en1));
  assign bankout = en3 ? out_9[31:24] : 8'bz;  // Controlled_Buffer controlled_buffer_4
  Pull_Resistor pull_resistor_4 (.node(en3));
  assign Q = en ? bankout : 8'bz;  // Controlled_Buffer controlled_buffer_5
  Pull_Resistor pull_resistor_5 (.node(en));

  // Other names for the same wires on the sheet: dataIn[7:0] = I; dgbankout[31:0] = out_9; r0[7:0] = out_9[7:0];
  //   r1[7:0] = out_9[15:8]; r2[7:0] = out_9[23:16]; r3[7:0] = out_9[31:24]; reset = res; selrreg[1:0] = regsel;
  //   selwreg[1:0] = wesel

  // Notes on the sheet:
  //   4 Bank 8-bit Registers 2 x select on reading & writing
endmodule

module constantbank (
  input  [2:0] regsel,
  input  en,
  output [7:0] Q
);

  wire en0, en1, en2, en3, en4, en5, en6, en7;
  wire [7:0] bankout;

  Decoder #(.select(3)) decoder_1 (
    .out0(en0), .out1(en1), .out2(en2), .out3(en3), .out4(en4), .out5(en5), .out6(en6), .out7(en7),
    .sel(regsel));  // open: en
  assign bankout = en0 ? {8{1'b0}} : 8'bz;  // Controlled_Buffer controlled_buffer_1
  assign bankout = en1 ? 8'h1 : 8'bz;  // Controlled_Buffer controlled_buffer_2
  assign bankout = en2 ? 8'h2 : 8'bz;  // Controlled_Buffer controlled_buffer_3
  assign bankout = en3 ? 8'h4 : 8'bz;  // Controlled_Buffer controlled_buffer_4
  assign bankout = en4 ? 8'h10 : 8'bz;  // Controlled_Buffer controlled_buffer_5
  assign bankout = en5 ? 8'hf0 : 8'bz;  // Controlled_Buffer controlled_buffer_6
  assign bankout = en6 ? 8'hf : 8'bz;  // Controlled_Buffer controlled_buffer_7
  assign bankout = en7 ? {8{1'b1}} : 8'bz;  // Controlled_Buffer controlled_buffer_8
  Pull_Resistor pull_resistor_1 (.node(en));
  assign Q = en ? bankout : 8'bz;  // Controlled_Buffer controlled_buffer_9

  // Other names for the same wires on the sheet: selreg[2:0] = regsel
endmodule

module rammodule (
  input  [15:0] addr,
  input  we,
  input  oe,
  input  clk,
  input  [7:0] din,
  output [7:0] dout
);

  wire [7:0] ram_1_data;

  RAM #(.addrWidth(16), .asyncread("true"), .databus("bidir")) ram_1 (
    .addr(addr), .we(we), .oe(oe), .clk(clk), .data(ram_1_data));
  assign ram_1_data = we ? din : 8'bz;  // Controlled_Buffer controlled_buffer_1
  assign dout = oe ? ram_1_data : 8'bz;  // Controlled_Buffer controlled_buffer_2
endmodule

module smallrammod (
  input  [15:0] addr,
  input  we,
  input  oe,
  input  clk,
  input  [7:0] din,
  output [7:0] dout
);

  wire clr, r0, r1, r2, r3, r4, r5, r6, r7, r8, r9, ra, rb, rc, rd, re, rf, we0, we1, we2, we3, we4, we5,
       we6, we7, we8, we9, wea, web, wec, wed, wee, wef;
  wire [7:0] \do , q0, q1, q2, q3, q4, q5, q6, q7, q8, q9, qa, qb, qc, qd, qe, qf;

  and and_1 (we0, we, r0);
  and and_2 (we1, we, r1);
  and and_3 (we2, we, r2);
  and and_4 (we3, we, r3);
  and and_5 (we4, we, r4);
  and and_6 (we5, we, r5);
  and and_7 (we6, we, r6);
  and and_8 (we7, we, r7);
  and and_9 (we8, we, r8);
  and and_10 (we9, we, r9);
  and and_11 (wea, we, ra);
  and and_12 (web, we, rb);
  and and_13 (wec, we, rc);
  and and_14 (wed, we, rd);
  and and_15 (wee, we, re);
  and and_16 (wef, we, rf);
  Register register_1 (.D(din), .en(we0), .clk(clk), .Q(q0), .clr(clr));
  Register register_2 (.D(din), .en(we2), .clk(clk), .Q(q2), .clr(clr));
  Register register_3 (.D(din), .en(we4), .clk(clk), .Q(q4), .clr(clr));
  Register register_4 (.D(din), .en(we6), .clk(clk), .Q(q6), .clr(clr));
  Register register_5 (.D(din), .en(we8), .clk(clk), .Q(q8), .clr(clr));
  Register register_6 (.D(din), .en(wea), .clk(clk), .Q(qa), .clr(clr));
  Register register_7 (.D(din), .en(wec), .clk(clk), .Q(qc), .clr(clr));
  Register register_8 (.D(din), .en(wee), .clk(clk), .Q(qe), .clr(clr));
  Register register_9 (.D(din), .en(wed), .clk(clk), .Q(qd), .clr(clr));
  Register register_10 (.D(din), .en(wef), .clk(clk), .Q(qf), .clr(clr));
  Register register_11 (.D(din), .en(we1), .clk(clk), .Q(q1), .clr(clr));
  Register register_12 (.D(din), .en(we3), .clk(clk), .Q(q3), .clr(clr));
  Register register_13 (.D(din), .en(we5), .clk(clk), .Q(q5), .clr(clr));
  Register register_14 (.D(din), .en(we7), .clk(clk), .Q(q7), .clr(clr));
  Register register_15 (.D(din), .en(we9), .clk(clk), .Q(q9), .clr(clr));
  Register register_16 (.D(din), .en(web), .clk(clk), .Q(qb), .clr(clr));
  and and_17 (r0, ~addr[3], ~addr[2], ~addr[1], ~addr[0]);  // AND_Gate
  and and_18 (r4, ~addr[3], addr[2], ~addr[1], ~addr[0]);  // AND_Gate
  and and_19 (r8, addr[3], ~addr[2], ~addr[1], ~addr[0]);  // AND_Gate
  and and_20 (rc, addr[3], addr[2], ~addr[1], ~addr[0]);  // AND_Gate
  assign \do  = r0 ? q0 : 8'bz;  // Controlled_Buffer controlled_buffer_1
  assign \do  = r1 ? q1 : 8'bz;  // Controlled_Buffer controlled_buffer_2
  assign \do  = r4 ? q4 : 8'bz;  // Controlled_Buffer controlled_buffer_3
  assign \do  = r5 ? q5 : 8'bz;  // Controlled_Buffer controlled_buffer_4
  assign \do  = r8 ? q8 : 8'bz;  // Controlled_Buffer controlled_buffer_5
  assign \do  = r9 ? q9 : 8'bz;  // Controlled_Buffer controlled_buffer_6
  assign \do  = rc ? qc : 8'bz;  // Controlled_Buffer controlled_buffer_7
  assign \do  = rd ? qd : 8'bz;  // Controlled_Buffer controlled_buffer_8
  and and_21 (r1, ~addr[3], ~addr[2], ~addr[1], addr[0]);  // AND_Gate
  and and_22 (r5, ~addr[3], addr[2], ~addr[1], addr[0]);  // AND_Gate
  and and_23 (r9, addr[3], ~addr[2], ~addr[1], addr[0]);  // AND_Gate
  and and_24 (rd, addr[3], addr[2], ~addr[1], addr[0]);  // AND_Gate
  assign \do  = r2 ? q2 : 8'bz;  // Controlled_Buffer controlled_buffer_9
  assign \do  = r3 ? q3 : 8'bz;  // Controlled_Buffer controlled_buffer_10
  assign \do  = r6 ? q6 : 8'bz;  // Controlled_Buffer controlled_buffer_11
  assign \do  = r7 ? q7 : 8'bz;  // Controlled_Buffer controlled_buffer_12
  assign \do  = ra ? qa : 8'bz;  // Controlled_Buffer controlled_buffer_13
  assign \do  = rb ? qb : 8'bz;  // Controlled_Buffer controlled_buffer_14
  assign \do  = re ? qe : 8'bz;  // Controlled_Buffer controlled_buffer_15
  assign \do  = rf ? qf : 8'bz;  // Controlled_Buffer controlled_buffer_16
  and and_25 (r2, ~addr[3], ~addr[2], addr[1], ~addr[0]);  // AND_Gate
  and and_26 (r6, ~addr[3], addr[2], addr[1], ~addr[0]);  // AND_Gate
  and and_27 (ra, addr[3], ~addr[2], addr[1], ~addr[0]);  // AND_Gate
  and and_28 (re, addr[3], addr[2], addr[1], ~addr[0]);  // AND_Gate
  assign dout = oe ? \do  : 8'bz;  // Controlled_Buffer controlled_buffer_17
  and and_29 (r3, ~addr[3], ~addr[2], addr[1], addr[0]);  // AND_Gate
  and and_30 (r7, ~addr[3], addr[2], addr[1], addr[0]);  // AND_Gate
  and and_31 (rb, addr[3], ~addr[2], addr[1], addr[0]);  // AND_Gate
  and and_32 (rf, addr[3], addr[2], addr[1], addr[0]);

  // Other names for the same wires on the sheet: a0 = addr[0]; a1 = addr[1]; a2 = addr[2]; a3 = addr[3]
endmodule

module ramrom (
  input  [15:0] addr,
  input  we,
  input  oe,
  input  clk,
  input  [7:0] din,
  output [7:0] dout
);

  wire [7:0] rom_1_data;

  ROM #(.addrWidth(16)) rom_1 (.addr(addr), .data(rom_1_data));
  assign dout = oe ? rom_1_data : 8'bz;  // Controlled_Buffer controlled_buffer_1

  // Notes on the sheet:
  //   contents of rom_1 (hex, n*v repeats v):
  //   f 1e e0 2d e0 2d e0 f0 5*0 1 42 23
endmodule

module bcd7seg (
  input  [3:0] value,
  input  en,
  output a,
  output b,
  output c,
  output d,
  output e,
  output f,
  output g,
  output dp
);

  wire AorB, as, bs, cs, ds, es, fs, gs, nA, nB, nC, nD;

  or or_1 (AorB, value[3], value[2]);
  or or_2 (cs, nC, value[0], value[2]);
  not not_1 (nA, value[3]);
  not not_2 (nB, value[2]);
  not not_3 (nC, value[1]);
  not not_4 (nD, value[0]);
  Multiplexer #(.enable("false"), .select(2)) multiplexer_1 (
    .in0(nB), .in1(AorB), .in2(nB), .in3(1'b1), .out(as), .sel(value[1:0]));
  Multiplexer #(.enable("false"), .select(2)) multiplexer_2 (
    .in0(1'b1), .in1(nB), .in2(nB), .in3(1'b1), .out(bs), .sel(value[1:0]));
  Multiplexer #(.enable("false"), .select(2)) multiplexer_3 (
    .in0(nB), .in1(value[2]), .in2(1'b1), .in3(nB), .out(ds), .sel(value[1:0]));
  Multiplexer #(.enable("false"), .select(2)) multiplexer_4 (
    .in0(nB), .in1(1'b0), .in2(1'b1), .in3(1'b0), .out(es), .sel(value[1:0]));
  Multiplexer #(.enable("false"), .select(2)) multiplexer_5 (
    .in0(1'b1), .in1(AorB), .in2(value[2]), .in3(1'b0), .out(fs), .sel(value[1:0]));
  Multiplexer #(.enable("false"), .select(2)) multiplexer_6 (
    .in0(AorB), .in1(AorB), .in2(1'b1), .in3(nB), .out(gs), .sel(value[1:0]));
  assign a = en ? as : 1'bz;  // Controlled_Buffer controlled_buffer_1
  assign b = en ? bs : 1'bz;  // Controlled_Buffer controlled_buffer_2
  assign c = en ? cs : 1'bz;  // Controlled_Buffer controlled_buffer_3
  assign d = en ? ds : 1'bz;  // Controlled_Buffer controlled_buffer_4
  assign e = en ? es : 1'bz;  // Controlled_Buffer controlled_buffer_5
  assign f = en ? fs : 1'bz;  // Controlled_Buffer controlled_buffer_6
  assign g = en ? gs : 1'bz;  // Controlled_Buffer controlled_buffer_7
  assign dp = en ? 1'b0 : 1'bz;  // Controlled_Buffer controlled_buffer_8

  // Other names for the same wires on the sheet: D_t = value[0]; sel[1:0] = value[1:0]; C_t = value[1];
  //   B_t = value[2]; A_t = value[3]

  // Notes on the sheet:
  //   BCD - 7-Seg Display Driver
  //   Digital Logic and Computer Organisation - RAJARAMAN et al - Johnny Brighton 2021
endmodule

module hex7seg (
  input  [3:0] value,
  input  dot,
  input  en,
  output a,
  output b,
  output c,
  output d,
  output e,
  output f,
  output g,
  output dp
);

  wire as, bs, cs, ds, es, fs, gs;
  wire [7:7] rom_1_data;

  ROM #(.addrWidth(4)) rom_1 (.addr(value), .data({rom_1_data[7], gs, fs, es, ds, cs, bs, as}));
  assign a = en ? as : 1'bz;  // Controlled_Buffer controlled_buffer_1
  assign b = en ? bs : 1'bz;  // Controlled_Buffer controlled_buffer_2
  assign c = en ? cs : 1'bz;  // Controlled_Buffer controlled_buffer_3
  assign d = en ? ds : 1'bz;  // Controlled_Buffer controlled_buffer_4
  assign e = en ? es : 1'bz;  // Controlled_Buffer controlled_buffer_5
  assign f = en ? fs : 1'bz;  // Controlled_Buffer controlled_buffer_6
  assign g = en ? gs : 1'bz;  // Controlled_Buffer controlled_buffer_7
  assign dp = en ? dot : 1'bz;  // Controlled_Buffer controlled_buffer_8

  // Other names for the same wires on the sheet: dp_t = dot

  // Notes on the sheet:
  //   contents of rom_1 (hex, n*v repeats v):
  //   3f 6 5b 4f 66 6d 7d 7 7f 6f 77 7c 39 5e 79 71
  //   HEX - 7-Seg Display Driver
  //   0:0x3f, 1:0x06, 2:0x5b, 3:0x4f, 4:0x66, 5:0x6d, 6:0x7d, 7:0x07, 8:7f, 9:0x6f, 10:0x77, 11:0x7c, 12:0x39, 13:0x5e, 14:0x79, 15:0x71
endmodule

module seg16hdisplay (
  input  reset,
  input  clk,
  input  [15:0] I,
  input  en,
  output [3:0] anode,
  output [7:0] hseg
);

  wire a, b, c, d, e, f, g, p, wclk;
  wire [3:0] nybble, Q;

  not not_1 (wclk, clk);
  assign nybble = Q[0] ? I[3:0] : 4'bz;  // Controlled_Buffer controlled_buffer_1
  assign nybble = Q[2] ? I[11:8] : 4'bz;  // Controlled_Buffer controlled_buffer_2
  assign nybble = Q[1] ? I[7:4] : 4'bz;  // Controlled_Buffer controlled_buffer_3
  assign nybble = Q[3] ? I[15:12] : 4'bz;  // Controlled_Buffer controlled_buffer_4
  hex7seg hex7seg_1 (.a(a), .b(b), .c(c), .d(d), .e(e), .f(f), .g(g), .dp(p), .en(en), .value(nybble));  // open: dot
  ring4 ring4_1 (.Q(Q), .clr(reset), .clk(clk));
  assign anode = en ? Q : 4'bz;  // Controlled_Buffer controlled_buffer_5
  assign hseg = en ? {g, f, a, b, e, d, c, p} : 8'bz;  // Controlled_Buffer controlled_buffer_6

  // Other names for the same wires on the sheet: clr = reset; Q1 = Q[0]; Q2 = Q[1]; Q3 = Q[2]; Q4 = Q[3];
  //   value16[15:0] = I
endmodule

module TESTaltHexDisplay (
);

  wire cpuCLKdiv2, H1, H2, H3, H4, uRESET;
  wire [3:0] b1s, b2s, b3s, b4s, bs, t1s, t2s, t3s, t4s, ts;

  _7_Segment_Display u_7_segment_display_1 (
    .g(t4s[3]), .f(t4s[2]), .a(t4s[1]), .b(t4s[0]), .e(b4s[3]), .d(b4s[2]), .c(b4s[1]), .dp(b4s[0]));
  _7_Segment_Display u_7_segment_display_2 (
    .g(t3s[3]), .f(t3s[2]), .a(t3s[1]), .b(t3s[0]), .e(b3s[3]), .d(b3s[2]), .c(b3s[1]), .dp(b3s[0]));
  _7_Segment_Display u_7_segment_display_3 (
    .g(t2s[3]), .f(t2s[2]), .a(t2s[1]), .b(t2s[0]), .e(b2s[3]), .d(b2s[2]), .c(b2s[1]), .dp(b2s[0]));
  _7_Segment_Display u_7_segment_display_4 (
    .g(t1s[3]), .f(t1s[2]), .a(t1s[1]), .b(t1s[0]), .e(b1s[3]), .d(b1s[2]), .c(b1s[1]), .dp(b1s[0]));
  // Probe on {H4, H3, H2, H1}
  assign t1s = H1 ? ts : 4'bz;  // Controlled_Buffer controlled_buffer_1
  assign b1s = H1 ? bs : 4'bz;  // Controlled_Buffer controlled_buffer_2
  seg16hdisplay seg16hdisplay_1 (
    .anode({H4, H3, H2, H1}), .hseg({ts, bs}), .I(16'h1234), .en(1'b1), .reset(uRESET), .clk(cpuCLKdiv2));
  // Probe on {ts, bs}
  assign t2s = H2 ? ts : 4'bz;  // Controlled_Buffer controlled_buffer_3
  assign b2s = H2 ? bs : 4'bz;  // Controlled_Buffer controlled_buffer_4
  assign t3s = H3 ? ts : 4'bz;  // Controlled_Buffer controlled_buffer_5
  assign b3s = H3 ? bs : 4'bz;  // Controlled_Buffer controlled_buffer_6
  assign t4s = H4 ? ts : 4'bz;  // Controlled_Buffer controlled_buffer_7
  assign b4s = H4 ? bs : 4'bz;  // Controlled_Buffer controlled_buffer_8
endmodule

module TESTALU (
  input  in_1,
  input  [7:0] in_2,
  input  [7:0] in_3,
  input  [2:0] in_4,
  output [7:0] out_5
);

  wire alu_1_c, alu_1_p, alu_1_s, alu_1_v, alu_1_z, and_1_out, and_2_out, and_3_out, and_4_out, and_5_out,
       and_6_out, and_7_out, and_8_out, pull_resistor_1_node;
  wire [5:0] alufnc;

  // Probe on in_3
  Pull_Resistor #(.pull(1)) pull_resistor_1 (.node(pull_resistor_1_node));
  // Probe on in_2
  and and_1 (and_1_out, ~alufnc[5], ~alufnc[4], alufnc[3], alufnc[2], ~alufnc[1], ~alufnc[0]);  // AND_Gate
  LED led_1 (.in(and_1_out));
  LED led_2 (.in(pull_resistor_1_node));
  alu alu_1 (
    .res(out_5), .C(alu_1_c), .Z(alu_1_z), .P(alu_1_p), .V(alu_1_v), .S(alu_1_s), .A(in_2), .B(in_3),
    .cin(in_1), .en(1'b1), .fn(alufnc));
  and and_2 (and_2_out, ~alufnc[5], ~alufnc[4], ~alufnc[3], ~alufnc[2], alufnc[1], alufnc[0]);  // AND_Gate
  LED led_3 (.in(and_2_out));
  // Probe on out_5
  LED led_4 (.in(alu_1_c));
  LED led_5 (.in(alu_1_z));
  LED led_6 (.in(alu_1_p));
  LED led_7 (.in(alu_1_v));
  LED led_8 (.in(alu_1_s));
  and and_3 (and_3_out, alufnc[5], ~alufnc[4], ~alufnc[3], ~alufnc[2], ~alufnc[1], ~alufnc[0]);  // AND_Gate
  LED led_9 (.in(and_3_out));
  and and_4 (and_4_out, ~alufnc[5], alufnc[4], ~alufnc[3], ~alufnc[2], ~alufnc[1], ~alufnc[0]);  // AND_Gate
  LED led_10 (.in(and_4_out));
  and and_5 (and_5_out, alufnc[5], alufnc[4], alufnc[3], ~alufnc[2], ~alufnc[1], ~alufnc[0]);  // AND_Gate
  LED led_11 (.in(and_5_out));
  and and_6 (and_6_out, alufnc[5], alufnc[4], alufnc[3], alufnc[2], alufnc[1], ~alufnc[0]);  // AND_Gate
  LED led_12 (.in(and_6_out));
  and and_7 (and_7_out, alufnc[5], alufnc[4], ~alufnc[3], alufnc[2], alufnc[1], ~alufnc[0]);  // AND_Gate
  LED led_13 (.in(and_7_out));
  // Probe on alufnc
  Multiplexer #(.enable("false"), .select(3), .width(6)) multiplexer_1 (
    .in0(6'b001100), .in1(6'b000011), .in2(6'b100000), .in3(6'b010000), .in4(6'b111000), .in5(6'b111110),
    .in6(6'b110110), .in7({6{1'b0}}), .out(alufnc), .sel(in_4));
  and and_8 (and_8_out, ~alufnc[5], ~alufnc[4], ~alufnc[3], ~alufnc[2], ~alufnc[1], ~alufnc[0]);  // AND_Gate
  LED led_14 (.in(and_8_out));

  // Other names for the same wires on the sheet: fncsel[2:0] = in_4

  // Notes on the sheet:
  //   ADD
  //   SUB
  //   SHIFT LEFT
  //   SHIFT RIGHT
  //   AND
  //   OR
  //   XOR
  //   NOP
endmodule

module TEST (
  input  [7:0] in_1,
  input  [7:0] in_2
);

  wire CLK, RESET_out, uRESET;
  wire [4:0] addr;
  wire [12:0] controller_1_addr;
  wire [19:0] Q;
  wire [31:0] controller_1_cntrl;

  controller controller_1 (
    .addr(controller_1_addr), .cntrl(controller_1_cntrl), .clr(uRESET), .opcode(in_2));  // open: Q, opdec, cpuCLK, ncpuCLK, CLK, nCLK, clkd2, pause
  Clock clock_1 (.out(CLK));
  // Probe on controller_1_addr
  // Probe on Q
  ring20 ring20_1 (.Q(Q), .clr(uRESET), .clk(CLK));
  // Probe on controller_1_cntrl
  Button RESET (.out(RESET_out));
  debounce debounce_1 (.resp(uRESET), .req(RESET_out), .clk(CLK));
  LED led_1 (.in(uRESET));
  assign addr = Q[0] ? {5{1'b0}} : 5'bz;  // Controlled_Buffer controlled_buffer_1
  assign addr = Q[1] ? 5'b00001 : 5'bz;  // Controlled_Buffer controlled_buffer_2
  assign addr = Q[2] ? 5'b00010 : 5'bz;  // Controlled_Buffer controlled_buffer_3
  assign addr = Q[3] ? 5'b00011 : 5'bz;  // Controlled_Buffer controlled_buffer_4
  assign addr = Q[4] ? 5'b00100 : 5'bz;  // Controlled_Buffer controlled_buffer_5
  assign addr = Q[5] ? 5'b00101 : 5'bz;  // Controlled_Buffer controlled_buffer_6
  assign addr = Q[6] ? 5'b00110 : 5'bz;  // Controlled_Buffer controlled_buffer_7
  assign addr = Q[7] ? 5'b00111 : 5'bz;  // Controlled_Buffer controlled_buffer_8
  assign addr = Q[8] ? 5'b01000 : 5'bz;  // Controlled_Buffer controlled_buffer_9
  assign addr = Q[9] ? 5'b01001 : 5'bz;  // Controlled_Buffer controlled_buffer_10
  assign addr = Q[10] ? 5'b01010 : 5'bz;  // Controlled_Buffer controlled_buffer_11
  assign addr = Q[11] ? 5'b01011 : 5'bz;  // Controlled_Buffer controlled_buffer_12
  assign addr = Q[12] ? 5'b01100 : 5'bz;  // Controlled_Buffer controlled_buffer_13
  assign addr = Q[13] ? 5'b01101 : 5'bz;  // Controlled_Buffer controlled_buffer_14
  assign addr = Q[14] ? 5'b01110 : 5'bz;  // Controlled_Buffer controlled_buffer_15
  assign addr = Q[15] ? 5'b01111 : 5'bz;  // Controlled_Buffer controlled_buffer_16
  assign addr = Q[16] ? 5'b10000 : 5'bz;  // Controlled_Buffer controlled_buffer_17
  assign addr = Q[17] ? 5'b10001 : 5'bz;  // Controlled_Buffer controlled_buffer_18
  assign addr = Q[18] ? 5'b10010 : 5'bz;  // Controlled_Buffer controlled_buffer_19
  assign addr = Q[19] ? 5'b10011 : 5'bz;  // Controlled_Buffer controlled_buffer_20
  assign addr = 1'b0 ? 5'b10100 : 5'bz;  // Controlled_Buffer controlled_buffer_21
  // Probe on {in_1, addr}
  ROM #(.addrWidth(13)) rom_1 (.addr({in_1, addr}));  // open: data
  // Probe on addr

  // Other names for the same wires on the sheet: addr[12:5] = in_1; Qd[4:0] = addr

  // Notes on the sheet:
  //   Qd is Log2(Q) * 1
endmodule
